// Digital circuit 16-Bit_Processor_Logical.dig as structural Verilog
module _16_Bit_Processor_Logical (
  input  [15:0] dBus,
  input  OUT_CLK,
  input  [15:0] iBus,
  input  Master_CLR,
  input  Master_Clock
);

  wire a, alu_1_co, alu_1_zero, b, branch_1_jmp, brWE, c, CLK, Co, d, dig1, dig2, dig3, dig4, e, f, g, hlt,
       imem, imm, immOE, memOE, memWE, nCLK, outEN, rdOE, rdWE, rs0WE, rs1WE, rs2OE, rs2WE, rs3OE, rs3WE, sf,
       Zo;
  wire [2:0] br;
  wire [5:0] aluOP;
  wire [7:0] imm_register_1_qimem;
  wire [15:0] alu_1_y, Branch_Register_q, imm_register_1_qimm, Out_Register_q, program_counter_1_pc, RD_q,
       RS0_q, RS1_q, RS2_q, RS3_q;
  wire [23:0] decoder_1_d;

  // Probe on iBus
  // Probe on iBus
  and and_1 (CLK, Master_Clock, ~hlt);  // And
  Program_Memory program_memory_1 (.OE(1'b1), .WE(1'b1), .A(program_counter_1_pc[11:0]), .CLK(CLK), .D(iBus));
  Imm_Register imm_register_1 (
    .IMEM(imem), .IMM(imm), .D(iBus), .CLK(CLK), .QIMM(imm_register_1_qimm), .QIMEM(imm_register_1_qimem));
  Decoder decoder_1 (
    .Rdest(iBus[3:0]), .Rsrc(iBus[7:4]), .OP(iBus[15:8]), .OE(1'b1), .WE(1'b0), .CE(1'b1),
    .D({rs3OE, rs2OE, rdOE, rs3WE, rs2WE, rdWE, rs1WE, rs0WE, decoder_1_d[23:21], brWE, br, sf, decoder_1_d[15:14], immOE, memWE, memOE, outEN, imem, imm, aluOP, hlt, decoder_1_d[0]}));
  // Probe on program_counter_1_pc
  // Probe on program_counter_1_pc
  not not_1 (nCLK, CLK);
  Branch branch_1 (.CTRL(br), .Z(Zo), .C(Co), .JMP(branch_1_jmp));
  _16_Bit_Register Branch_Register (.D(iBus), .CLK(CLK), .EN(brWE), .Q(Branch_Register_q));
  // Probe on Branch_Register_q
  // Probe on Branch_Register_q
  Program_Counter program_counter_1 (
    .CLK(CLK), .CLR(Master_CLR), .LD(branch_1_jmp), .EN(1'b1), .D(Branch_Register_q),
    .PC(program_counter_1_pc));
  assign dBus = immOE ? imm_register_1_qimm : 16'bz;  // Driver driver_1
  // Probe on {rs3OE, rs2OE, rdOE, rs3WE, rs2WE, rdWE, rs1WE, rs0WE, decoder_1_d[23:21], brWE, br, sf, decoder_1_d[15:14], immOE, memWE, memOE, outEN, imem, imm, aluOP, hlt, decoder_1_d[0]}
  _16_Bit_Register RS0 (.D(dBus), .CLK(CLK), .EN(rs0WE), .Q(RS0_q));
  // Probe on RS0_q
  // Probe on RS0_q
  _16_Bit_Register RS1 (.D(dBus), .CLK(CLK), .EN(rs1WE), .Q(RS1_q));
  // Probe on RS1_q
  // Probe on RS1_q
  RAM ram_1 (.OE(memOE), .WE(memWE), .A(imm_register_1_qimem), .CLK(CLK), .D(dBus));
  ALU alu_1 (.A(RS0_q), .B(RS1_q), .aluOP(aluOP), .Y(alu_1_y), .ZERO(alu_1_zero), .Co(alu_1_co));
  Flags_Register flags_register_1 (.Ci(alu_1_co), .Zi(alu_1_zero), .CLK(CLK), .EN(sf), .Co(Co), .Zo(Zo));
  // Probe on alu_1_y
  // Probe on alu_1_y
  // Probe on RD_q
  // Probe on RD_q
  // Probe on Out_Register_q
  // Probe on Out_Register_q
  _16_Bit_Register RD (.D(alu_1_y), .CLK(CLK), .EN(rdWE), .Q(RD_q));
  Output_Decoder output_decoder_1 (
    .Q(Out_Register_q), .OUT_CLK(OUT_CLK), .a(a), .b(b), .c(c), .d(d), .e(e), .f(f), .g(g), .dig1(dig1),
    .dig2(dig2), .dig3(dig3), .dig4(dig4));
  _16_Bit_Register Out_Register (.D(dBus), .CLK(CLK), .EN(outEN), .Q(Out_Register_q));
  assign dBus = rdOE ? RD_q : 16'bz;  // Driver driver_2
  Seven_Seg #(.commonCathode("true")) seven_seg_1 (
    .a(a), .b(b), .c(c), .d(d), .e(e), .f(f), .g(g), .dp(1'b0), .common(dig1));
  Seven_Seg #(.commonCathode("true")) seven_seg_2 (
    .a(a), .b(b), .c(c), .d(d), .e(e), .f(f), .g(g), .dp(1'b0), .common(dig2));
  assign dBus = rs2OE ? RS2_q : 16'bz;  // Driver driver_3
  assign dBus = rs3OE ? RS3_q : 16'bz;  // Driver driver_4
  Seven_Seg #(.commonCathode("true")) seven_seg_3 (
    .a(a), .b(b), .c(c), .d(d), .e(e), .f(f), .g(g), .dp(1'b0), .common(dig3));
  Seven_Seg #(.commonCathode("true")) seven_seg_4 (
    .a(a), .b(b), .c(c), .d(d), .e(e), .f(f), .g(g), .dp(1'b0), .common(dig4));
  // Probe on RS2_q
  // Probe on RS2_q
  _16_Bit_Register RS2 (.D(dBus), .CLK(CLK), .EN(rs2WE), .Q(RS2_q));
  // Probe on RS3_q
  // Probe on RS3_q
  _16_Bit_Register RS3 (.D(dBus), .CLK(CLK), .EN(rs3WE), .Q(RS3_q));

  // Other names for the same wires on the sheet: CLR = Master_CLR

  // Notes on the sheet:
  //   OUT_CLK: Hz: 20
  //   16-Bit Instruction Bus
  //   16-Bit Data Bus
endmodule
