// Digital circuit 16-Bit_Register.dig as structural Verilog
module _16_Bit_Register (
  input  [15:0] D,
  input  CLK,
  input  EN,
  output [15:0] Q
);

  Register #(.Bits(16)) register_1 (.D(D), .C(CLK), .en(EN), .Q(Q));

  // Notes on the sheet:
  //   Inputs/Outputs
endmodule
