// Digital circuit 8-Bit_Register.dig as structural Verilog
module _8_Bit_Register (
  input  [15:0] D,
  input  CLK,
  input  EN,
  output [15:0] Q
);

  Register #(.Bits(8)) register_1 (.D(D[7:0]), .C(CLK), .en(EN), .Q(Q[7:0]));
  // Pins of 8 and 16 bits meet at D
  // Pins of 8 and 16 bits meet at Q

  // Notes on the sheet:
  //   Inputs/Outputs
endmodule
