// Digital circuit ALU.dig as structural Verilog
module ALU (
  input  [15:0] A,
  input  [15:0] B,
  input  [5:0] aluOP,
  output [15:0] Y,
  output ZERO,
  output Co
);

  wire ADD, ADDI, AND, ANDI, OR, or_2_out, or_3_out, or_4_out, or_5_out, ORI, ROL, ROR, SLD, SLL, SRL, SUB,
       SUBI, XOR;
  wire [3:0] Ysel;
  wire [15:0] add_1_s, and_1_out, or_1_out, Rotate_Left_out, Rotate_Right_out, Shift_Left_out,
       Shift_Right_out, sub_1_s, xor_1_out;

  // Probe on Y
  Add #(.Bits(16)) add_1 (.a(A), .b(B), .c_i(1'b0), .s(add_1_s), .c_o(Co));
  Sub #(.Bits(16)) sub_1 (.a(A), .b(B), .c_i(1'b0), .s(sub_1_s));  // open: c_o
  assign and_1_out = A & B;  // And and_1, 16 bits wide
  assign or_1_out = A | B;  // Or or_1, 16 bits wide
  assign xor_1_out = A ^ B;  // XOr xor_1, 16 bits wide
  BarrelShifter #(.Bits(16)) Shift_Left (.in(A), .shift(5'b00001), .out(Shift_Left_out));
  BarrelShifter #(.Bits(16), .direction("right")) Shift_Right (.in(A), .shift(5'b00001), .out(Shift_Right_out));
  BarrelShifter #(.Bits(16), .barrelShifterMode("rotate")) Rotate_Left (
    .in(A), .shift(5'b00001), .out(Rotate_Left_out));
  BarrelShifter #(.Bits(16), .barrelShifterMode("rotate"), .direction("right")) Rotate_Right (
    .in(A), .shift(5'b00001), .out(Rotate_Right_out));
  Comparator #(.Bits(16)) comparator_1 (.a(A), .b({16{1'b0}}), .eq(ZERO));  // open: gt, lt
  Multiplexer #(.Selector_Bits(4), .Bits(16)) multiplexer_1 (
    .sel(Ysel), .in_0(add_1_s), .in_1(sub_1_s), .in_2(and_1_out), .in_3(or_1_out), .in_4(xor_1_out),
    .in_5(Shift_Left_out), .in_6(Shift_Right_out), .in_7(Rotate_Left_out), .in_8(Rotate_Right_out),
    .in_9({16{1'b0}}), .in_10({16{1'b0}}), .in_11({16{1'b0}}), .in_12({16{1'b0}}), .in_13({16{1'b0}}),
    .in_14({16{1'b0}}), .in_15({16{1'b0}}), .out(Y));
  Decoder #(.Selector_Bits(4)) decoder_1 (
    .sel(aluOP[3:0]), .out_1(ADD), .out_2(SUB), .out_3(ADDI), .out_4(SUBI), .out_5(AND), .out_6(OR),
    .out_7(XOR), .out_8(ANDI), .out_9(ORI), .out_10(SLL), .out_11(SRL), .out_12(ROL), .out_13(ROR),
    .out_14(SLD));  // open: out_0, out_15
  or or_2 (or_2_out, ADD, ADDI);
  or or_3 (or_3_out, SUB, SUBI);
  or or_4 (or_4_out, AND, ANDI);
  or or_5 (or_5_out, OR, ORI);
  PriorityEncoder #(.Selector_Bits(4)) priorityencoder_1 (
    .in0(or_2_out), .in1(or_3_out), .in2(or_4_out), .in3(or_5_out), .in4(XOR), .in5(SLL), .in6(SRL),
    .in7(ROL), .in8(ROR), .in9(1'b0), .in10(1'b0), .in11(1'b0), .in12(1'b0), .in13(1'b0), .in14(1'b0),
    .in15(1'b0), .num(Ysel));  // open: any

  // Notes on the sheet:
  //   Comparator Unit
  //   Math Unit
  //   Shift Unit
endmodule
