// Digital circuit Branch.dig as structural Verilog
module Branch (
  input  [2:0] CTRL,
  input  Z,
  input  C,
  output JMP
);

  wire multiplexer_1_out;

  Multiplexer #(.Selector_Bits(2)) multiplexer_1 (
    .sel(CTRL[1:0]), .in_0(1'b0), .in_1(Z), .in_2(C), .in_3(1'b0), .out(multiplexer_1_out));
  xor xor_1 (JMP, multiplexer_1_out, CTRL[2]);

  // Notes on the sheet:
  //   Branch Control Logic
  //   C2 C1 C0 Operation
  //   0    0    0    Noop
  //   0    0    1    Branch if Carry (C)
  //   0    1    0    Branch if Zero (Z)
  //   1    x    x    Jump (J)
endmodule
