// Digital circuit Decoder.dig as structural Verilog
module Decoder (
  input  [3:0] Rdest,
  input  [3:0] Rsrc,
  input  [7:0] OP,
  input  OE,
  input  WE,
  input  CE,
  output [31:0] D
);

  wire or_1_out;
  wire [7:0] A;

  EEPROM #(.AddrBits(8), .Bits(8)) DEC_ROM0 (.A(A), .CS(CE), .WE(WE), .OE(OE), .D(D[7:0]));
  EEPROM #(.AddrBits(8), .Bits(8)) DEC_ROM1 (.A(A), .CS(CE), .WE(WE), .OE(OE), .D(D[15:8]));
  EEPROM #(.AddrBits(8), .Bits(8)) DEC_ROM2 (.A(A), .CS(CE), .WE(WE), .OE(OE), .D(D[23:16]));
  Decoder #(.Selector_Bits(3)) decoder_1 (
    .sel(Rdest[2:0]), .out_1(D[24]), .out_2(D[25]), .out_3(D[26]), .out_4(D[27]), .out_5(D[28]));  // open: out_0, out_6, out_7
  or or_1 (or_1_out, D[8], D[9]);
  Multiplexer #(.Bits(8)) multiplexer_1 (.sel(or_1_out), .in_0(OP), .in_1({8{1'b0}}), .out(A));
  Decoder #(.Selector_Bits(3)) decoder_2 (
    .sel(Rsrc[2:0]), .out_1(D[29]), .out_2(D[30]), .out_3(D[31]));  // open: out_0, out_4, out_5, out_6, out_7

  // Other names for the same wires on the sheet: D0[7:0] = D[7:0]; D1[7:0] = D[15:8]; imm = D[8]; imem = D[9];
  //   D2[7:0] = D[23:16]; rdOE = D[29]; reg[7:0] = D[31:24]; rdWE = D[26]; rs0WE = D[24]; rs1WE = D[25];
  //   rs2OE = D[30]; rs2WE = D[27]; rs3OE = D[31]; rs3WE = D[28]

  // Notes on the sheet:
  //   I/O
  //   Decoder ROMs
  //   Force nop if imm OR imem is set
  //   Register Address Decoder
endmodule
