// Digital circuit Flags_Register.dig as structural Verilog
module Flags_Register (
  input  Ci,
  input  Zi,
  input  CLK,
  input  EN,
  output Co,
  output Zo
);

  wire [7:2] Q;

  Register #(.Bits(8)) register_1 (.D({{6{1'b0}}, Zi, Ci}), .C(CLK), .en(EN), .Q({Q, Zo, Co}));

  // Other names for the same wires on the sheet: D[1:0] = {Zi, Ci}; Q[1:0] = {Zo, Co}

  // Notes on the sheet:
  //   Inputs/Outputs
endmodule
