// Digital circuit Imm_Register.dig as structural Verilog
module Imm_Register (
  input  IMEM,
  input  IMM,
  input  [15:0] D,
  input  CLK,
  output [15:0] QIMM,
  output [7:0] QIMEM
);

  wire or_1_out;

  or or_1 (or_1_out, IMM, IMEM);
  _16_Bit_Register _16_bit_register_1 (.D(D), .CLK(CLK), .EN(or_1_out), .Q({QIMM[15:8], QIMEM}));

  assign QIMM[7:0] = QIMEM;

  // Other names for the same wires on the sheet: Q[15:0] = {QIMM[15:8], QIMEM}
endmodule
