// Digital circuit Output_Decoder.dig as structural Verilog
module Output_Decoder (
  input  [15:0] Q,
  input  OUT_CLK,
  output a,
  output b,
  output c,
  output d,
  output e,
  output f,
  output g,
  output dig1,
  output dig2,
  output dig3,
  output dig4
);

  wire [1:0] counter_1_out;
  wire [3:0] multiplexer_1_out;

  Counter #(.Bits(2)) counter_1 (.en(1'b1), .C(OUT_CLK), .clr(1'b0), .out(counter_1_out));  // open: ovf
  Multiplexer #(.Selector_Bits(2), .Bits(4)) multiplexer_1 (
    .sel(counter_1_out), .in_0(Q[3:0]), .in_1(Q[7:4]), .in_2(Q[11:8]), .in_3(Q[15:12]),
    .out(multiplexer_1_out));
  Decoder #(.Selector_Bits(2)) decoder_1 (.sel(counter_1_out), .out_0(dig1), .out_1(dig2), .out_2(dig3), .out_3(dig4));
  EEPROM #(.AddrBits(4), .Bits(7)) OUT_ROM (
    .A(multiplexer_1_out), .CS(1'b1), .WE(1'b0), .OE(1'b1), .D({g, f, e, d, c, b, a}));
  Seven_Seg #(.commonCathode("true")) seven_seg_1 (
    .a(a), .b(b), .c(c), .d(d), .e(e), .f(f), .g(g), .dp(1'b0), .common(dig1));
  Seven_Seg #(.commonCathode("true")) seven_seg_2 (
    .a(a), .b(b), .c(c), .d(d), .e(e), .f(f), .g(g), .dp(1'b0), .common(dig2));
  Seven_Seg #(.commonCathode("true")) seven_seg_3 (
    .a(a), .b(b), .c(c), .d(d), .e(e), .f(f), .g(g), .dp(1'b0), .common(dig3));
  Seven_Seg #(.commonCathode("true")) seven_seg_4 (
    .a(a), .b(b), .c(c), .d(d), .e(e), .f(f), .g(g), .dp(1'b0), .common(dig4));

  // Notes on the sheet:
  //   OUT_CLK: Hz: 20
  //   contents of OUT_ROM (hex, n*v repeats v):
  //   3f,6,5b,4f,66,6d,7d,7,7f,6f,77,7c,39,5e,79,71
  //   contents of OUT-ROM (hex, n*v repeats v):
  //   3f,6,5b,4f,66,6d,7d,7,7f,6f,77,7c,39,5e,79,71
endmodule
