// Digital circuit Program_Counter.dig as structural Verilog
module Program_Counter (
  input  CLK,
  input  CLR,
  input  LD,
  input  EN,
  input  [15:0] D,
  output [15:0] PC
);

  CounterPreset #(.Bits(16)) counterpreset_1 (
    .en(EN), .C(CLK), .dir(1'b0), .in(D), .ld(LD), .clr(CLR), .out(PC));  // open: ovf

  // Notes on the sheet:
  //   CLK: Hz: 5
  //   EN: default 1
endmodule
