// Digital circuit Program_Memory.dig as structural Verilog
module Program_Memory (
  input  OE,
  input  WE,
  input  [11:0] A,
  input  CLK,
  output [15:0] D
);

  RAMSinglePort #(.AddrBits(12), .isProgramMemory("true"), .Bits(16)) ramsingleport_1 (
    .A(A), .str(WE), .C(CLK), .ld(OE), .D(D));
endmodule
