// Digital circuit RAM.dig as structural Verilog
module RAM (
  input  OE,
  input  WE,
  input  [7:0] A,
  input  CLK,
  output [15:0] D
);

  RAMSinglePort #(.AddrBits(8), .Bits(16)) ramsingleport_1 (.A(A), .str(WE), .C(CLK), .ld(OE), .D(D));
endmodule
