// Digital circuit 16_Bit_Driver.dig as structural Verilog
module _16_Bit_Driver (
  input  A0,
  input  A1,
  input  A2,
  input  A3,
  input  A4,
  input  A5,
  input  A6,
  input  A7,
  input  A8,
  input  A9,
  input  A10,
  input  A11,
  input  A12,
  input  A13,
  input  A14,
  input  A15,
  input  nOE,
  input  DIR,
  output B0,
  output B1,
  output B2,
  output B3,
  output B4,
  output B5,
  output B6,
  output B7,
  output B8,
  output B9,
  output B10,
  output B11,
  output B12,
  output B13,
  output B14,
  output B15
);

  _74245 LO (
    .pin1(DIR), .pin2(A0), .pin3(A1), .pin4(A2), .pin5(A3), .pin6(A4), .pin7(A5), .pin8(A6), .pin9(A7),
    .pin10(1'b0), .pin11(B7), .pin12(B6), .pin13(B5), .pin14(B4), .pin15(B3), .pin16(B2), .pin17(B1),
    .pin18(B0), .pin19(nOE), .pin20(1'b1));
  _74245 HI (
    .pin1(DIR), .pin2(A8), .pin3(A9), .pin4(A10), .pin5(A11), .pin6(A12), .pin7(A13), .pin8(A14), .pin9(A15),
    .pin10(1'b0), .pin11(B15), .pin12(B14), .pin13(B13), .pin14(B12), .pin15(B11), .pin16(B10), .pin17(B9),
    .pin18(B8), .pin19(nOE), .pin20(1'b1));

  // Notes on the sheet:
  //   DIR: DIR = 0, A <- B
  //   DIR = 0, A -> B, default 1
endmodule
