// Digital circuit 16_Bit_Processor_Schematic.dig as structural Verilog
module _16_Bit_Processor_Schematic (
  input  Master_Clock,
  input  Master_Clear,
  input  OUT_CLK,
  input  in_4,
  input  [15:0] iBus,
  input  [15:0] dBus,
  input  dBusEn
);

  wire _16_bit_driver_1_b0, _16_bit_driver_1_b1, _16_bit_driver_1_b2, _16_bit_driver_1_b3,
       _16_bit_driver_1_b4, _16_bit_driver_1_b5, _16_bit_driver_1_b6, _16_bit_driver_1_b7,
       _16_bit_driver_1_b8, _16_bit_driver_1_b9, _16_bit_driver_1_b10, _16_bit_driver_1_b11,
       _16_bit_driver_1_b12, _16_bit_driver_1_b13, _16_bit_driver_1_b14, _16_bit_driver_1_b15, alu_1_alu0,
       alu_1_alu1, alu_1_alu2, alu_1_alu3, alu_1_alu4, alu_1_alu5, alu_1_alu6, alu_1_alu7, alu_1_alu8,
       alu_1_alu9, alu_1_alu10, alu_1_alu11, alu_1_alu12, alu_1_alu13, alu_1_alu14, alu_1_alu15,
       branch_1_njmp, Branch_Register_q0, Branch_Register_q1, Branch_Register_q2, Branch_Register_q3,
       Branch_Register_q4, Branch_Register_q5, Branch_Register_q6, Branch_Register_q7, Branch_Register_q8,
       Branch_Register_q9, Branch_Register_q10, Branch_Register_q11, Branch_Register_q12,
       Branch_Register_q13, Branch_Register_q14, Branch_Register_q15, brWE, bussplitter_1_d0,
       bussplitter_1_d1, bussplitter_1_d2, bussplitter_1_d3, bussplitter_1_d4, bussplitter_1_d5,
       bussplitter_1_d6, bussplitter_1_d7, bussplitter_1_d8, bussplitter_1_d9, bussplitter_1_d10,
       bussplitter_1_d11, bussplitter_1_d12, bussplitter_1_d13, bussplitter_1_d14, bussplitter_1_d15, Carry,
       CLK, Co, display_decoder_v2_1_a, display_decoder_v2_1_b, display_decoder_v2_1_c,
       display_decoder_v2_1_d, display_decoder_v2_1_dig1, display_decoder_v2_1_dig2,
       display_decoder_v2_1_dig3, display_decoder_v2_1_dig4, display_decoder_v2_1_e, display_decoder_v2_1_f,
       display_decoder_v2_1_g, hlt, imem, imm, ImRegister_qimem0, ImRegister_qimem1, ImRegister_qimem2,
       ImRegister_qimem3, ImRegister_qimem4, ImRegister_qimem5, ImRegister_qimem6, ImRegister_qimem7,
       ImRegister_qimm0, ImRegister_qimm1, ImRegister_qimm2, ImRegister_qimm3, ImRegister_qimm4,
       ImRegister_qimm5, ImRegister_qimm6, ImRegister_qimm7, ImRegister_qimm8, ImRegister_qimm9,
       ImRegister_qimm10, ImRegister_qimm11, ImRegister_qimm12, ImRegister_qimm13, ImRegister_qimm14,
       ImRegister_qimm15, nCLK, nimmOE, nmemOE, nmemWE, nrdOE, nrs2OE, nrs3OE, outEN, rdWE, rs0WE, rs1WE,
       rs2WE, rs3WE, sf, Zero, Zo;
  wire [0:0] decoder_1_d;
  wire [2:0] br;
  wire [5:0] aluOP;
  wire [7:5] decoder_1_d_3;
  wire [7:6] decoder_1_d_2;
  wire [11:0] mon_pc;
  wire [15:0] mon_rd, mon_rs0, mon_rs1, mon_rs2, mon_rs3;

  // Probe on {nrs3OE, nrs2OE, nrdOE, rs3WE, rs2WE, rdWE, rs1WE, rs0WE, decoder_1_d_3, brWE, br, sf, decoder_1_d_2, nimmOE, nmemWE, nmemOE, outEN, imem, imm, aluOP, hlt, decoder_1_d[0]}
  BusSplitter #(.Bits(16)) bussplitter_1 (
    .D(iBus), .OE(in_4), .D0(bussplitter_1_d0), .D1(bussplitter_1_d1), .D2(bussplitter_1_d2),
    .D3(bussplitter_1_d3), .D4(bussplitter_1_d4), .D5(bussplitter_1_d5), .D6(bussplitter_1_d6),
    .D7(bussplitter_1_d7), .D8(bussplitter_1_d8), .D9(bussplitter_1_d9), .D10(bussplitter_1_d10),
    .D11(bussplitter_1_d11), .D12(bussplitter_1_d12), .D13(bussplitter_1_d13), .D14(bussplitter_1_d14),
    .D15(bussplitter_1_d15));
  Decoder decoder_1 (
    .nOE(1'b0), .nCE(1'b0), .nWE(1'b1), .Rdest0(bussplitter_1_d0), .Rdest1(bussplitter_1_d1),
    .Rdest2(bussplitter_1_d2), .Rdest3(bussplitter_1_d3), .Rsrc0(bussplitter_1_d4), .Rsrc1(bussplitter_1_d5),
    .Rsrc2(bussplitter_1_d6), .Rsrc3(bussplitter_1_d7), .OP0(bussplitter_1_d8), .OP1(bussplitter_1_d9),
    .OP2(bussplitter_1_d10), .OP3(bussplitter_1_d11), .OP4(bussplitter_1_d12), .OP5(bussplitter_1_d13),
    .OP6(bussplitter_1_d14), .OP7(bussplitter_1_d15),
    .D({nrs3OE, nrs2OE, nrdOE, rs3WE, rs2WE, rdWE, rs1WE, rs0WE, decoder_1_d_3, brWE, br, sf, decoder_1_d_2, nimmOE, nmemWE, nmemOE, outEN, imem, imm, aluOP, hlt, decoder_1_d[0]}));
  ImRegister ImRegister (
    .D0(bussplitter_1_d0), .D1(bussplitter_1_d1), .D2(bussplitter_1_d2), .D3(bussplitter_1_d3),
    .D4(bussplitter_1_d4), .D5(bussplitter_1_d5), .D6(bussplitter_1_d6), .D7(bussplitter_1_d7),
    .D8(bussplitter_1_d8), .D9(bussplitter_1_d9), .D10(bussplitter_1_d10), .D11(bussplitter_1_d11),
    .D12(bussplitter_1_d12), .D13(bussplitter_1_d13), .D14(bussplitter_1_d14), .D15(bussplitter_1_d15),
    .CLK(CLK), .IMM(imm), .IMEM(imem), .QIMM0(ImRegister_qimm0), .QIMM1(ImRegister_qimm1),
    .QIMM2(ImRegister_qimm2), .QIMM3(ImRegister_qimm3), .QIMM4(ImRegister_qimm4), .QIMM5(ImRegister_qimm5),
    .QIMM6(ImRegister_qimm6), .QIMM7(ImRegister_qimm7), .QIMM8(ImRegister_qimm8), .QIMM9(ImRegister_qimm9),
    .QIMM10(ImRegister_qimm10), .QIMM11(ImRegister_qimm11), .QIMM12(ImRegister_qimm12),
    .QIMM13(ImRegister_qimm13), .QIMM14(ImRegister_qimm14), .QIMM15(ImRegister_qimm15),
    .QIMEM0(ImRegister_qimem0), .QIMEM1(ImRegister_qimem1), .QIMEM2(ImRegister_qimem2),
    .QIMEM3(ImRegister_qimem3), .QIMEM4(ImRegister_qimem4), .QIMEM5(ImRegister_qimem5),
    .QIMEM6(ImRegister_qimem6), .QIMEM7(ImRegister_qimem7));
  Program_Memory_v2 program_memory_v2_1 (
    .A0(mon_pc[0]), .A1(mon_pc[1]), .A2(mon_pc[2]), .A3(mon_pc[3]), .A4(mon_pc[4]), .A5(mon_pc[5]),
    .A6(mon_pc[6]), .A7(mon_pc[7]), .A8(mon_pc[8]), .A9(mon_pc[9]), .A10(mon_pc[10]), .A11(mon_pc[11]),
    .nWE(1'b1), .nOE(1'b0), .D0(bussplitter_1_d0), .D1(bussplitter_1_d1), .D2(bussplitter_1_d2),
    .D3(bussplitter_1_d3), .D4(bussplitter_1_d4), .D5(bussplitter_1_d5), .D6(bussplitter_1_d6),
    .D7(bussplitter_1_d7), .D8(bussplitter_1_d8), .D9(bussplitter_1_d9), .D10(bussplitter_1_d10),
    .D11(bussplitter_1_d11), .D12(bussplitter_1_d12), .D13(bussplitter_1_d13), .D14(bussplitter_1_d14),
    .D15(bussplitter_1_d15));
  Branch branch_1 (.Z(Zo), .C(Co), .CTRL0(br[0]), .CTRL1(br[1]), .CTRL2(br[2]), .njmp(branch_1_njmp));
  _16_Bit_Register Branch_Register (
    .D0(bussplitter_1_d0), .D1(bussplitter_1_d1), .D2(bussplitter_1_d2), .D3(bussplitter_1_d3),
    .D4(bussplitter_1_d4), .D5(bussplitter_1_d5), .D6(bussplitter_1_d6), .D7(bussplitter_1_d7),
    .D8(bussplitter_1_d8), .D9(bussplitter_1_d9), .D10(bussplitter_1_d10), .D11(bussplitter_1_d11),
    .D12(bussplitter_1_d12), .D13(bussplitter_1_d13), .D14(bussplitter_1_d14), .D15(bussplitter_1_d15),
    .EN(brWE), .CLK(CLK), .nCLR(1'b1), .Q0(Branch_Register_q0), .Q1(Branch_Register_q1),
    .Q2(Branch_Register_q2), .Q3(Branch_Register_q3), .Q4(Branch_Register_q4), .Q5(Branch_Register_q5),
    .Q6(Branch_Register_q6), .Q7(Branch_Register_q7), .Q8(Branch_Register_q8), .Q9(Branch_Register_q9),
    .Q10(Branch_Register_q10), .Q11(Branch_Register_q11), .Q12(Branch_Register_q12),
    .Q13(Branch_Register_q13), .Q14(Branch_Register_q14), .Q15(Branch_Register_q15));
  _16_Bit_Driver _16_bit_driver_1 (
    .A0(ImRegister_qimm0), .A1(ImRegister_qimm1), .A2(ImRegister_qimm2), .A3(ImRegister_qimm3),
    .A4(ImRegister_qimm4), .A5(ImRegister_qimm5), .A6(ImRegister_qimm6), .A7(ImRegister_qimm7),
    .A8(ImRegister_qimm8), .A9(ImRegister_qimm9), .A10(ImRegister_qimm10), .A11(ImRegister_qimm11),
    .A12(ImRegister_qimm12), .A13(ImRegister_qimm13), .A14(ImRegister_qimm14), .A15(ImRegister_qimm15),
    .nOE(nimmOE), .DIR(1'b1), .B0(_16_bit_driver_1_b0), .B1(_16_bit_driver_1_b1), .B2(_16_bit_driver_1_b2),
    .B3(_16_bit_driver_1_b3), .B4(_16_bit_driver_1_b4), .B5(_16_bit_driver_1_b5), .B6(_16_bit_driver_1_b6),
    .B7(_16_bit_driver_1_b7), .B8(_16_bit_driver_1_b8), .B9(_16_bit_driver_1_b9), .B10(_16_bit_driver_1_b10),
    .B11(_16_bit_driver_1_b11), .B12(_16_bit_driver_1_b12), .B13(_16_bit_driver_1_b13),
    .B14(_16_bit_driver_1_b14), .B15(_16_bit_driver_1_b15));
  // Probe on mon_rs0
  // Probe on mon_rs1
  // Probe on mon_rs2
  // Probe on mon_rs3
  // Probe on mon_rd
  // Probe on mon_rd
  // Probe on mon_pc
  PC pc_1 (
    .CLK(CLK), .nCLR(Master_Clear), .nEN(1'b0), .nLD(branch_1_njmp), .D15(Branch_Register_q15),
    .D14(Branch_Register_q14), .D13(Branch_Register_q13), .D12(Branch_Register_q12),
    .D11(Branch_Register_q11), .D10(Branch_Register_q10), .D9(Branch_Register_q9), .D8(Branch_Register_q8),
    .D7(Branch_Register_q7), .D6(Branch_Register_q6), .D5(Branch_Register_q5), .D4(Branch_Register_q4),
    .D3(Branch_Register_q3), .D2(Branch_Register_q2), .D1(Branch_Register_q1), .D0(Branch_Register_q0),
    .PC0(mon_pc[0]), .PC1(mon_pc[1]), .PC2(mon_pc[2]), .PC3(mon_pc[3]), .PC4(mon_pc[4]), .PC5(mon_pc[5]),
    .PC6(mon_pc[6]), .PC7(mon_pc[7]), .PC8(mon_pc[8]), .PC9(mon_pc[9]), .PC10(mon_pc[10]), .PC11(mon_pc[11]));  // open: CO, PC12, PC13, PC14, PC15
  // Probe on Zero
  // Probe on Carry
  and and_1 (CLK, Master_Clock, ~hlt);  // And
  not not_1 (nCLK, CLK);
  BusSplitter #(.Bits(16)) bussplitter_2 (
    .D(dBus), .OE(dBusEn), .D0(_16_bit_driver_1_b0), .D1(_16_bit_driver_1_b1), .D2(_16_bit_driver_1_b2),
    .D3(_16_bit_driver_1_b3), .D4(_16_bit_driver_1_b4), .D5(_16_bit_driver_1_b5), .D6(_16_bit_driver_1_b6),
    .D7(_16_bit_driver_1_b7), .D8(_16_bit_driver_1_b8), .D9(_16_bit_driver_1_b9), .D10(_16_bit_driver_1_b10),
    .D11(_16_bit_driver_1_b11), .D12(_16_bit_driver_1_b12), .D13(_16_bit_driver_1_b13),
    .D14(_16_bit_driver_1_b14), .D15(_16_bit_driver_1_b15));
  RAM ram_1 (
    .D0(_16_bit_driver_1_b0), .D1(_16_bit_driver_1_b1), .D2(_16_bit_driver_1_b2), .D3(_16_bit_driver_1_b3),
    .D4(_16_bit_driver_1_b4), .D5(_16_bit_driver_1_b5), .D6(_16_bit_driver_1_b6), .D7(_16_bit_driver_1_b7),
    .D8(_16_bit_driver_1_b8), .D9(_16_bit_driver_1_b9), .D10(_16_bit_driver_1_b10),
    .D11(_16_bit_driver_1_b11), .D12(_16_bit_driver_1_b12), .D13(_16_bit_driver_1_b13),
    .D14(_16_bit_driver_1_b14), .D15(_16_bit_driver_1_b15), .nWE(nmemWE), .nOE(nmemOE), .nCE(1'b0),
    .A0(ImRegister_qimem0), .A1(ImRegister_qimem1), .A2(ImRegister_qimem2), .A3(ImRegister_qimem3),
    .A4(ImRegister_qimem4), .A5(ImRegister_qimem5), .A6(ImRegister_qimem6), .A7(ImRegister_qimem7));
  _16_Bit_Register RS0 (
    .D0(_16_bit_driver_1_b0), .D1(_16_bit_driver_1_b1), .D2(_16_bit_driver_1_b2), .D3(_16_bit_driver_1_b3),
    .D4(_16_bit_driver_1_b4), .D5(_16_bit_driver_1_b5), .D6(_16_bit_driver_1_b6), .D7(_16_bit_driver_1_b7),
    .D8(_16_bit_driver_1_b8), .D9(_16_bit_driver_1_b9), .D10(_16_bit_driver_1_b10),
    .D11(_16_bit_driver_1_b11), .D12(_16_bit_driver_1_b12), .D13(_16_bit_driver_1_b13),
    .D14(_16_bit_driver_1_b14), .D15(_16_bit_driver_1_b15), .EN(rs0WE), .CLK(nCLK), .nCLR(1'b1),
    .Q0(mon_rs0[0]), .Q1(mon_rs0[1]), .Q2(mon_rs0[2]), .Q3(mon_rs0[3]), .Q4(mon_rs0[4]), .Q5(mon_rs0[5]),
    .Q6(mon_rs0[6]), .Q7(mon_rs0[7]), .Q8(mon_rs0[8]), .Q9(mon_rs0[9]), .Q10(mon_rs0[10]), .Q11(mon_rs0[11]),
    .Q12(mon_rs0[12]), .Q13(mon_rs0[13]), .Q14(mon_rs0[14]), .Q15(mon_rs0[15]));
  _16_Bit_Register RS1 (
    .D0(_16_bit_driver_1_b0), .D1(_16_bit_driver_1_b1), .D2(_16_bit_driver_1_b2), .D3(_16_bit_driver_1_b3),
    .D4(_16_bit_driver_1_b4), .D5(_16_bit_driver_1_b5), .D6(_16_bit_driver_1_b6), .D7(_16_bit_driver_1_b7),
    .D8(_16_bit_driver_1_b8), .D9(_16_bit_driver_1_b9), .D10(_16_bit_driver_1_b10),
    .D11(_16_bit_driver_1_b11), .D12(_16_bit_driver_1_b12), .D13(_16_bit_driver_1_b13),
    .D14(_16_bit_driver_1_b14), .D15(_16_bit_driver_1_b15), .EN(rs1WE), .CLK(nCLK), .nCLR(1'b1),
    .Q0(mon_rs1[0]), .Q1(mon_rs1[1]), .Q2(mon_rs1[2]), .Q3(mon_rs1[3]), .Q4(mon_rs1[4]), .Q5(mon_rs1[5]),
    .Q6(mon_rs1[6]), .Q7(mon_rs1[7]), .Q8(mon_rs1[8]), .Q9(mon_rs1[9]), .Q10(mon_rs1[10]), .Q11(mon_rs1[11]),
    .Q12(mon_rs1[12]), .Q13(mon_rs1[13]), .Q14(mon_rs1[14]), .Q15(mon_rs1[15]));
  LED D14 (.in(_16_bit_driver_1_b14));
  LED D15 (.in(_16_bit_driver_1_b15));
  Seven_Seg #(.commonCathode("true")) seven_seg_1 (
    .a(display_decoder_v2_1_a), .b(display_decoder_v2_1_b), .c(display_decoder_v2_1_c),
    .d(display_decoder_v2_1_d), .e(display_decoder_v2_1_e), .f(display_decoder_v2_1_f),
    .g(display_decoder_v2_1_g), .dp(1'b0), .common(display_decoder_v2_1_dig1));
  LED D10 (.in(_16_bit_driver_1_b10));
  LED D11 (.in(_16_bit_driver_1_b11));
  LED D12 (.in(_16_bit_driver_1_b12));
  LED D13 (.in(_16_bit_driver_1_b13));
  LED D6 (.in(_16_bit_driver_1_b6));
  LED D7 (.in(_16_bit_driver_1_b7));
  LED D8 (.in(_16_bit_driver_1_b8));
  LED D9 (.in(_16_bit_driver_1_b9));
  // Probe on mon_rs0
  // Probe on mon_rs1
  Seven_Seg #(.commonCathode("true")) seven_seg_2 (
    .a(display_decoder_v2_1_a), .b(display_decoder_v2_1_b), .c(display_decoder_v2_1_c),
    .d(display_decoder_v2_1_d), .e(display_decoder_v2_1_e), .f(display_decoder_v2_1_f),
    .g(display_decoder_v2_1_g), .dp(1'b0), .common(display_decoder_v2_1_dig2));
  LED D2 (.in(_16_bit_driver_1_b2));
  LED D3 (.in(_16_bit_driver_1_b3));
  LED D4 (.in(_16_bit_driver_1_b4));
  LED D5 (.in(_16_bit_driver_1_b5));
  Seven_Seg #(.commonCathode("true")) seven_seg_3 (
    .a(display_decoder_v2_1_a), .b(display_decoder_v2_1_b), .c(display_decoder_v2_1_c),
    .d(display_decoder_v2_1_d), .e(display_decoder_v2_1_e), .f(display_decoder_v2_1_f),
    .g(display_decoder_v2_1_g), .dp(1'b0), .common(display_decoder_v2_1_dig3));
  LED D0 (.in(_16_bit_driver_1_b0));
  LED D1 (.in(_16_bit_driver_1_b1));
  ALU alu_1 (
    .Ci(Co), .CLK(CLK), .nCLR(Master_Clear), .A0(mon_rs0[0]), .A1(mon_rs0[1]), .A2(mon_rs0[2]),
    .A3(mon_rs0[3]), .A4(mon_rs0[4]), .A5(mon_rs0[5]), .A6(mon_rs0[6]), .A7(mon_rs0[7]), .A8(mon_rs0[8]),
    .A9(mon_rs0[9]), .A10(mon_rs0[10]), .A11(mon_rs0[11]), .A12(mon_rs0[12]), .A13(mon_rs0[13]),
    .A14(mon_rs0[14]), .A15(mon_rs0[15]), .OP0(aluOP[0]), .OP1(aluOP[1]), .OP2(aluOP[2]), .OP3(aluOP[3]),
    .OP4(aluOP[4]), .OP5(aluOP[5]), .B0(mon_rs1[0]), .B1(mon_rs1[1]), .B2(mon_rs1[2]), .B3(mon_rs1[3]),
    .B4(mon_rs1[4]), .B5(mon_rs1[5]), .B6(mon_rs1[6]), .B7(mon_rs1[7]), .B8(mon_rs1[8]), .B9(mon_rs1[9]),
    .B10(mon_rs1[10]), .B11(mon_rs1[11]), .B12(mon_rs1[12]), .B13(mon_rs1[13]), .B14(mon_rs1[14]),
    .B15(mon_rs1[15]), .ALU0(alu_1_alu0), .ALU1(alu_1_alu1), .ALU2(alu_1_alu2), .ALU3(alu_1_alu3),
    .ALU4(alu_1_alu4), .ALU5(alu_1_alu5), .ALU6(alu_1_alu6), .ALU7(alu_1_alu7), .ALU8(alu_1_alu8),
    .ALU9(alu_1_alu9), .ALU10(alu_1_alu10), .ALU11(alu_1_alu11), .ALU12(alu_1_alu12), .ALU13(alu_1_alu13),
    .ALU14(alu_1_alu14), .ALU15(alu_1_alu15), .Carry(Carry), .Zero(Zero));
  Seven_Seg #(.commonCathode("true")) seven_seg_4 (
    .a(display_decoder_v2_1_a), .b(display_decoder_v2_1_b), .c(display_decoder_v2_1_c),
    .d(display_decoder_v2_1_d), .e(display_decoder_v2_1_e), .f(display_decoder_v2_1_f),
    .g(display_decoder_v2_1_g), .dp(1'b0), .common(display_decoder_v2_1_dig4));
  _16_Bit_Register RD (
    .D0(alu_1_alu0), .D1(alu_1_alu1), .D2(alu_1_alu2), .D3(alu_1_alu3), .D4(alu_1_alu4), .D5(alu_1_alu5),
    .D6(alu_1_alu6), .D7(alu_1_alu7), .D8(alu_1_alu8), .D9(alu_1_alu9), .D10(alu_1_alu10), .D11(alu_1_alu11),
    .D12(alu_1_alu12), .D13(alu_1_alu13), .D14(alu_1_alu14), .D15(alu_1_alu15), .EN(rdWE), .CLK(CLK),
    .nCLR(1'b1), .Q0(mon_rd[0]), .Q1(mon_rd[1]), .Q2(mon_rd[2]), .Q3(mon_rd[3]), .Q4(mon_rd[4]),
    .Q5(mon_rd[5]), .Q6(mon_rd[6]), .Q7(mon_rd[7]), .Q8(mon_rd[8]), .Q9(mon_rd[9]), .Q10(mon_rd[10]),
    .Q11(mon_rd[11]), .Q12(mon_rd[12]), .Q13(mon_rd[13]), .Q14(mon_rd[14]), .Q15(mon_rd[15]));
  Flags_Register flags_register_1 (.Ci(Carry), .Zi(Zero), .CLK(CLK), .nCLR(Master_Clear), .store(sf), .Zo(Zo), .Co(Co));
  Display_Decoder_v2 display_decoder_v2_1 (
    .D15(_16_bit_driver_1_b15), .D14(_16_bit_driver_1_b14), .D13(_16_bit_driver_1_b13),
    .D12(_16_bit_driver_1_b12), .D11(_16_bit_driver_1_b11), .D10(_16_bit_driver_1_b10),
    .D9(_16_bit_driver_1_b9), .D8(_16_bit_driver_1_b8), .D7(_16_bit_driver_1_b7), .D6(_16_bit_driver_1_b6),
    .D5(_16_bit_driver_1_b5), .D4(_16_bit_driver_1_b4), .D3(_16_bit_driver_1_b3), .D2(_16_bit_driver_1_b2),
    .D1(_16_bit_driver_1_b1), .D0(_16_bit_driver_1_b0), .WE(outEN), .nCLR(1'b1), .CLK(CLK),
    .OUT_CLK(OUT_CLK), .g(display_decoder_v2_1_g), .f(display_decoder_v2_1_f), .e(display_decoder_v2_1_e),
    .d(display_decoder_v2_1_d), .c(display_decoder_v2_1_c), .b(display_decoder_v2_1_b),
    .a(display_decoder_v2_1_a), .dig1(display_decoder_v2_1_dig1), .dig2(display_decoder_v2_1_dig2),
    .dig3(display_decoder_v2_1_dig3), .dig4(display_decoder_v2_1_dig4));
  // Probe on mon_rd
  _16_Bit_Driver _16_bit_driver_2 (
    .A0(mon_rd[0]), .A1(mon_rd[1]), .A2(mon_rd[2]), .A3(mon_rd[3]), .A4(mon_rd[4]), .A5(mon_rd[5]),
    .A6(mon_rd[6]), .A7(mon_rd[7]), .A8(mon_rd[8]), .A9(mon_rd[9]), .A10(mon_rd[10]), .A11(mon_rd[11]),
    .A12(mon_rd[12]), .A13(mon_rd[13]), .A14(mon_rd[14]), .A15(mon_rd[15]), .nOE(nrdOE), .DIR(1'b1),
    .B0(_16_bit_driver_1_b0), .B1(_16_bit_driver_1_b1), .B2(_16_bit_driver_1_b2), .B3(_16_bit_driver_1_b3),
    .B4(_16_bit_driver_1_b4), .B5(_16_bit_driver_1_b5), .B6(_16_bit_driver_1_b6), .B7(_16_bit_driver_1_b7),
    .B8(_16_bit_driver_1_b8), .B9(_16_bit_driver_1_b9), .B10(_16_bit_driver_1_b10),
    .B11(_16_bit_driver_1_b11), .B12(_16_bit_driver_1_b12), .B13(_16_bit_driver_1_b13),
    .B14(_16_bit_driver_1_b14), .B15(_16_bit_driver_1_b15));
  _16_Bit_Register RS2 (
    .D0(_16_bit_driver_1_b0), .D1(_16_bit_driver_1_b1), .D2(_16_bit_driver_1_b2), .D3(_16_bit_driver_1_b3),
    .D4(_16_bit_driver_1_b4), .D5(_16_bit_driver_1_b5), .D6(_16_bit_driver_1_b6), .D7(_16_bit_driver_1_b7),
    .D8(_16_bit_driver_1_b8), .D9(_16_bit_driver_1_b9), .D10(_16_bit_driver_1_b10),
    .D11(_16_bit_driver_1_b11), .D12(_16_bit_driver_1_b12), .D13(_16_bit_driver_1_b13),
    .D14(_16_bit_driver_1_b14), .D15(_16_bit_driver_1_b15), .EN(rs2WE), .CLK(nCLK), .nCLR(1'b1),
    .Q0(mon_rs2[0]), .Q1(mon_rs2[1]), .Q2(mon_rs2[2]), .Q3(mon_rs2[3]), .Q4(mon_rs2[4]), .Q5(mon_rs2[5]),
    .Q6(mon_rs2[6]), .Q7(mon_rs2[7]), .Q8(mon_rs2[8]), .Q9(mon_rs2[9]), .Q10(mon_rs2[10]), .Q11(mon_rs2[11]),
    .Q12(mon_rs2[12]), .Q13(mon_rs2[13]), .Q14(mon_rs2[14]), .Q15(mon_rs2[15]));
  _16_Bit_Register RS3 (
    .D0(_16_bit_driver_1_b0), .D1(_16_bit_driver_1_b1), .D2(_16_bit_driver_1_b2), .D3(_16_bit_driver_1_b3),
    .D4(_16_bit_driver_1_b4), .D5(_16_bit_driver_1_b5), .D6(_16_bit_driver_1_b6), .D7(_16_bit_driver_1_b7),
    .D8(_16_bit_driver_1_b8), .D9(_16_bit_driver_1_b9), .D10(_16_bit_driver_1_b10),
    .D11(_16_bit_driver_1_b11), .D12(_16_bit_driver_1_b12), .D13(_16_bit_driver_1_b13),
    .D14(_16_bit_driver_1_b14), .D15(_16_bit_driver_1_b15), .EN(rs3WE), .CLK(nCLK), .nCLR(1'b1),
    .Q0(mon_rs3[0]), .Q1(mon_rs3[1]), .Q2(mon_rs3[2]), .Q3(mon_rs3[3]), .Q4(mon_rs3[4]), .Q5(mon_rs3[5]),
    .Q6(mon_rs3[6]), .Q7(mon_rs3[7]), .Q8(mon_rs3[8]), .Q9(mon_rs3[9]), .Q10(mon_rs3[10]), .Q11(mon_rs3[11]),
    .Q12(mon_rs3[12]), .Q13(mon_rs3[13]), .Q14(mon_rs3[14]), .Q15(mon_rs3[15]));
  // Probe on mon_rs2
  _16_Bit_Driver _16_bit_driver_3 (
    .A0(mon_rs2[0]), .A1(mon_rs2[1]), .A2(mon_rs2[2]), .A3(mon_rs2[3]), .A4(mon_rs2[4]), .A5(mon_rs2[5]),
    .A6(mon_rs2[6]), .A7(mon_rs2[7]), .A8(mon_rs2[8]), .A9(mon_rs2[9]), .A10(mon_rs2[10]), .A11(mon_rs2[11]),
    .A12(mon_rs2[12]), .A13(mon_rs2[13]), .A14(mon_rs2[14]), .A15(mon_rs2[15]), .nOE(nrs2OE), .DIR(1'b1),
    .B0(_16_bit_driver_1_b0), .B1(_16_bit_driver_1_b1), .B2(_16_bit_driver_1_b2), .B3(_16_bit_driver_1_b3),
    .B4(_16_bit_driver_1_b4), .B5(_16_bit_driver_1_b5), .B6(_16_bit_driver_1_b6), .B7(_16_bit_driver_1_b7),
    .B8(_16_bit_driver_1_b8), .B9(_16_bit_driver_1_b9), .B10(_16_bit_driver_1_b10),
    .B11(_16_bit_driver_1_b11), .B12(_16_bit_driver_1_b12), .B13(_16_bit_driver_1_b13),
    .B14(_16_bit_driver_1_b14), .B15(_16_bit_driver_1_b15));
  // Probe on mon_rs3
  _16_Bit_Driver _16_bit_driver_4 (
    .A0(mon_rs3[0]), .A1(mon_rs3[1]), .A2(mon_rs3[2]), .A3(mon_rs3[3]), .A4(mon_rs3[4]), .A5(mon_rs3[5]),
    .A6(mon_rs3[6]), .A7(mon_rs3[7]), .A8(mon_rs3[8]), .A9(mon_rs3[9]), .A10(mon_rs3[10]), .A11(mon_rs3[11]),
    .A12(mon_rs3[12]), .A13(mon_rs3[13]), .A14(mon_rs3[14]), .A15(mon_rs3[15]), .nOE(nrs3OE), .DIR(1'b1),
    .B0(_16_bit_driver_1_b0), .B1(_16_bit_driver_1_b1), .B2(_16_bit_driver_1_b2), .B3(_16_bit_driver_1_b3),
    .B4(_16_bit_driver_1_b4), .B5(_16_bit_driver_1_b5), .B6(_16_bit_driver_1_b6), .B7(_16_bit_driver_1_b7),
    .B8(_16_bit_driver_1_b8), .B9(_16_bit_driver_1_b9), .B10(_16_bit_driver_1_b10),
    .B11(_16_bit_driver_1_b11), .B12(_16_bit_driver_1_b12), .B13(_16_bit_driver_1_b13),
    .B14(_16_bit_driver_1_b14), .B15(_16_bit_driver_1_b15));

  // Other names for the same wires on the sheet: OP0 = aluOP[0]; OP1 = aluOP[1]; OP2 = aluOP[2]; OP3 = aluOP[3];
  //   OP4 = aluOP[4]; OP5 = aluOP[5]; nCLR = Master_Clear

  // Notes on the sheet:
  //   Master_Clock: Hz: 10
  //   Master_Clear: default 1
  //   OUT_CLK: Hz: 20
  //   in_4: default 1
  //   iBus: default 1
  //   16-Bit Instruction Bus
  //   16-Bit Data Bus Monitor
  //   contents of DEC-ROM0 (hex, n*v repeats v):
  //   0,2,2,8*0,84,88,8c,90,94,98,9c,a0,a4,68,6c,70,74,78
  //   contents of OUT-ROM (hex, n*v repeats v):
  //   3f,6,5b,4f,66,6d,7d,7,7f,6f,77,7c,39,5e,79,71
  //   contents of DEC-ROM2 (hex, n*v repeats v):
  //   8*0,13,14,18
  //   contents of DEC-ROM1 (hex, n*v repeats v):
  //   4*0,21,12,a,29,5*0,21,21,0,0,0,21,21,5*0,4
endmodule
