// Digital circuit 16_Bit_Register.dig as structural Verilog
module _16_Bit_Register (
  input  D0,
  input  D1,
  input  D2,
  input  D3,
  input  D4,
  input  D5,
  input  D6,
  input  D7,
  input  D8,
  input  D9,
  input  D10,
  input  D11,
  input  D12,
  input  D13,
  input  D14,
  input  D15,
  input  EN,
  input  CLK,
  input  nCLR,
  output Q0,
  output Q1,
  output Q2,
  output Q3,
  output Q4,
  output Q5,
  output Q6,
  output Q7,
  output Q8,
  output Q9,
  output Q10,
  output Q11,
  output Q12,
  output Q13,
  output Q14,
  output Q15
);

  wire LO_pin11;

  _74273 LO (
    .pin1(nCLR), .pin2(Q0), .pin3(D0), .pin4(D1), .pin5(Q1), .pin6(Q2), .pin7(D2), .pin8(D3), .pin9(Q3),
    .pin10(1'b0), .pin11(LO_pin11), .pin12(Q4), .pin13(D4), .pin14(D5), .pin15(Q5), .pin16(Q6), .pin17(D6),
    .pin18(D7), .pin19(Q7), .pin20(1'b1));
  _74273 HI (
    .pin1(nCLR), .pin2(Q8), .pin3(D8), .pin4(D9), .pin5(Q9), .pin6(Q10), .pin7(D10), .pin8(D11), .pin9(Q11),
    .pin10(1'b0), .pin11(LO_pin11), .pin12(Q12), .pin13(D12), .pin14(D13), .pin15(Q13), .pin16(Q14),
    .pin17(D14), .pin18(D15), .pin19(Q15), .pin20(1'b1));
  _7408 Dual_2in_AND (
    .pin1(EN), .pin2(CLK), .pin3(LO_pin11), .pin4(1'b0), .pin5(1'b0), .pin7(1'b0), .pin9(1'b0), .pin10(1'b0),
    .pin12(1'b0), .pin13(1'b0), .pin14(1'b1));  // open: pin6, pin8, pin11

  // Notes on the sheet:
  //   EN: default 1
  //   nCLR: default 1
endmodule
