// Digital circuit 16_Bit_Shift-Register.dig as structural Verilog
module _16_Bit_Shift_Register (
  input  S0,
  input  nCLR,
  input  CLK,
  input  OE,
  input  S1,
  input  B0,
  input  B1,
  input  B2,
  input  B3,
  input  B4,
  input  B5,
  input  B6,
  input  B7,
  input  B8,
  input  B9,
  input  B10,
  input  B11,
  input  B12,
  input  B13,
  input  B14,
  input  B15,
  input  ROR,
  input  ROL,
  input  DIR
);

  wire HI_pin4, HI_pin5, HI_pin6, HI_pin7, HI_pin8, HI_pin11, HI_pin13, HI_pin14, HI_pin15, HI_pin16,
       HI_pin17, HI_pin18, LO_pin4, LO_pin5, LO_pin6, LO_pin7, LO_pin8, LO_pin11, LO_pin13, LO_pin14,
       LO_pin15, LO_pin16;

  _74299 HI (
    .pin1(S0), .pin2(1'b0), .pin3(1'b0), .pin4(HI_pin4), .pin5(HI_pin5), .pin6(HI_pin6), .pin7(HI_pin7),
    .pin8(HI_pin8), .pin9(nCLR), .pin10(1'b0), .pin11(HI_pin11), .pin12(CLK), .pin13(HI_pin13),
    .pin14(HI_pin14), .pin15(HI_pin15), .pin16(HI_pin16), .pin17(HI_pin17), .pin18(HI_pin18), .pin19(S1),
    .pin20(1'b1));
  _74299 LO (
    .pin1(S0), .pin2(1'b0), .pin3(1'b0), .pin4(LO_pin4), .pin5(LO_pin5), .pin6(LO_pin6), .pin7(LO_pin7),
    .pin8(LO_pin8), .pin9(nCLR), .pin10(1'b0), .pin11(LO_pin11), .pin12(CLK), .pin13(LO_pin13),
    .pin14(LO_pin14), .pin15(LO_pin15), .pin16(LO_pin16), .pin17(HI_pin11), .pin18(HI_pin8), .pin19(S1),
    .pin20(1'b1));
  _74245 HI_2 (
    .pin1(DIR), .pin2(HI_pin7), .pin3(HI_pin13), .pin4(HI_pin6), .pin5(HI_pin14), .pin6(HI_pin5),
    .pin7(HI_pin15), .pin8(HI_pin4), .pin9(HI_pin16), .pin10(1'b0), .pin11(B15), .pin12(B14), .pin13(B13),
    .pin14(B12), .pin15(B11), .pin16(B10), .pin17(B9), .pin18(B8), .pin19(OE), .pin20(1'b1));
  _74245 LO_2 (
    .pin1(DIR), .pin2(LO_pin7), .pin3(LO_pin13), .pin4(LO_pin6), .pin5(LO_pin14), .pin6(LO_pin5),
    .pin7(LO_pin15), .pin8(LO_pin4), .pin9(LO_pin16), .pin10(1'b0), .pin11(B6), .pin12(B7), .pin13(B5),
    .pin14(B4), .pin15(B3), .pin16(B2), .pin17(B1), .pin18(B0), .pin19(OE), .pin20(1'b1));
  _7408 _4x2xAND (
    .pin1(ROR), .pin2(LO_pin8), .pin3(HI_pin18), .pin4(ROL), .pin5(HI_pin17), .pin6(LO_pin11), .pin7(1'b0),
    .pin9(1'b0), .pin10(1'b0), .pin12(1'b0), .pin13(1'b0), .pin14(1'b1));  // open: pin8, pin11

  // Notes on the sheet:
  //   nCLR: default 1
  //   Function Select
  //   Load S0=H, S1=H
  //   SRL S0=L, S1=H
  //   SLL S0=H, S1=L
  //   ROL S0=L, S1=H, ROL=1
  //   ROR S0=H, S1=L, ROR=1
endmodule
