// Digital circuit ALU.dig as structural Verilog
module ALU (
  input  Ci,
  input  CLK,
  input  nCLR,
  input  A0,
  input  A1,
  input  A2,
  input  A3,
  input  A4,
  input  A5,
  input  A6,
  input  A7,
  input  A8,
  input  A9,
  input  A10,
  input  A11,
  input  A12,
  input  A13,
  input  A14,
  input  A15,
  input  OP0,
  input  OP1,
  input  OP2,
  input  OP3,
  input  OP4,
  input  OP5,
  input  B0,
  input  B1,
  input  B2,
  input  B3,
  input  B4,
  input  B5,
  input  B6,
  input  B7,
  input  B8,
  input  B9,
  input  B10,
  input  B11,
  input  B12,
  input  B13,
  input  B14,
  input  B15,
  output ALU0,
  output ALU1,
  output ALU2,
  output ALU3,
  output ALU4,
  output ALU5,
  output ALU6,
  output ALU7,
  output ALU8,
  output ALU9,
  output ALU10,
  output ALU11,
  output ALU12,
  output ALU13,
  output ALU14,
  output ALU15,
  output Carry,
  output Zero
);

  wire nADD, nADDI, nADDs, nAND, nANDI, nANDs, nBOR, nOE0, nOE1, nOR, nORI, nORs, nROL, nROR, nSLD, nSLL,
       nSRL, nSUB, nSUBI, nXOR;
  wire [15:0] mon_math_unit, mon_sft_unit;

  Shift_Unit shift_unit_1 (
    .A0(A0), .A1(A1), .A2(A2), .A3(A3), .A4(A4), .A5(A5), .A6(A6), .A7(A7), .A8(A8), .A9(A9), .A10(A10),
    .A11(A11), .A12(A12), .A13(A13), .A14(A14), .A15(A15), .nCLR(nCLR), .CLK(CLK), .nSLL(nSLL), .nSRL(nSRL),
    .nROR(nROR), .nROL(nROL), .nSLD(nSLD), .Y0(mon_sft_unit[0]), .Y1(mon_sft_unit[1]), .Y2(mon_sft_unit[2]),
    .Y3(mon_sft_unit[3]), .Y4(mon_sft_unit[4]), .Y5(mon_sft_unit[5]), .Y6(mon_sft_unit[6]),
    .Y7(mon_sft_unit[7]), .Y8(mon_sft_unit[8]), .Y9(mon_sft_unit[9]), .Y10(mon_sft_unit[10]),
    .Y11(mon_sft_unit[11]), .Y12(mon_sft_unit[12]), .Y13(mon_sft_unit[13]), .Y14(mon_sft_unit[14]),
    .Y15(mon_sft_unit[15]));
  Math_Unit math_unit_1 (
    .A0(A0), .A1(A1), .A2(A2), .A3(A3), .A4(A4), .A5(A5), .A6(A6), .A7(A7), .A8(A8), .A9(A9), .A10(A10),
    .A11(A11), .A12(A12), .A13(A13), .A14(A14), .A15(A15), .B0(B0), .B1(B1), .B2(B2), .B3(B3), .B4(B4),
    .B5(B5), .B6(B6), .B7(B7), .B8(B8), .B9(B9), .B10(B10), .B11(B11), .B12(B12), .B13(B13), .B14(B14),
    .B15(B15), .Ci(Ci), .nBOR(nBOR), .nADDs(nADDs), .nSUBs(nBOR), .nANDs(nANDs), .nORs(nORs), .nXOR(nXOR),
    .Y0(mon_math_unit[0]), .Y1(mon_math_unit[1]), .Y2(mon_math_unit[2]), .Y3(mon_math_unit[3]),
    .Y4(mon_math_unit[4]), .Y5(mon_math_unit[5]), .Y6(mon_math_unit[6]), .Y7(mon_math_unit[7]),
    .Y8(mon_math_unit[8]), .Y9(mon_math_unit[9]), .Y10(mon_math_unit[10]), .Y11(mon_math_unit[11]),
    .Y12(mon_math_unit[12]), .Y13(mon_math_unit[13]), .Y14(mon_math_unit[14]), .Y15(mon_math_unit[15]),
    .C(Carry));
  Comparator_Unit comparator_unit_1 (
    .A0(A0), .A1(A1), .A2(A2), .A3(A3), .A4(A4), .A5(A5), .A6(A6), .A7(A7), .A8(A8), .A9(A9), .A10(A10),
    .A11(A11), .A12(A12), .A13(A13), .A14(A14), .A15(A15), .Zero(Zero));
  // Probe on mon_sft_unit
  // Probe on mon_math_unit
  _7404 Hex_Inv (
    .pin1(1'b0), .pin3(1'b0), .pin5(1'b0), .pin7(1'b0), .pin8(nOE1), .pin9(OP4), .pin10(nOE0), .pin11(OP5),
    .pin13(1'b0), .pin14(1'b1));  // open: pin2, pin4, pin6, pin12
  _16_Bit_Driver Shift_Unit_Out (
    .A0(mon_sft_unit[0]), .A1(mon_sft_unit[1]), .A2(mon_sft_unit[2]), .A3(mon_sft_unit[3]),
    .A4(mon_sft_unit[4]), .A5(mon_sft_unit[5]), .A6(mon_sft_unit[6]), .A7(mon_sft_unit[7]),
    .A8(mon_sft_unit[8]), .A9(mon_sft_unit[9]), .A10(mon_sft_unit[10]), .A11(mon_sft_unit[11]),
    .A12(mon_sft_unit[12]), .A13(mon_sft_unit[13]), .A14(mon_sft_unit[14]), .A15(mon_sft_unit[15]),
    .nOE(nOE1), .DIR(1'b1), .B0(ALU0), .B1(ALU1), .B2(ALU2), .B3(ALU3), .B4(ALU4), .B5(ALU5), .B6(ALU6),
    .B7(ALU7), .B8(ALU8), .B9(ALU9), .B10(ALU10), .B11(ALU11), .B12(ALU12), .B13(ALU13), .B14(ALU14),
    .B15(ALU15));
  _16_Bit_Driver Math_Unit_Out (
    .A0(mon_math_unit[0]), .A1(mon_math_unit[1]), .A2(mon_math_unit[2]), .A3(mon_math_unit[3]),
    .A4(mon_math_unit[4]), .A5(mon_math_unit[5]), .A6(mon_math_unit[6]), .A7(mon_math_unit[7]),
    .A8(mon_math_unit[8]), .A9(mon_math_unit[9]), .A10(mon_math_unit[10]), .A11(mon_math_unit[11]),
    .A12(mon_math_unit[12]), .A13(mon_math_unit[13]), .A14(mon_math_unit[14]), .A15(mon_math_unit[15]),
    .nOE(nOE0), .DIR(1'b1), .B0(ALU0), .B1(ALU1), .B2(ALU2), .B3(ALU3), .B4(ALU4), .B5(ALU5), .B6(ALU6),
    .B7(ALU7), .B8(ALU8), .B9(ALU9), .B10(ALU10), .B11(ALU11), .B12(ALU12), .B13(ALU13), .B14(ALU14),
    .B15(ALU15));
  _74154 _4_to_16_Encode (
    .pin2(nADD), .pin3(nSUB), .pin4(nADDI), .pin5(nSUBI), .pin6(nAND), .pin7(nOR), .pin8(nXOR), .pin9(nANDI),
    .pin10(nORI), .pin11(nSLL), .pin12(1'b0), .pin13(nSRL), .pin14(nROL), .pin15(nROR), .pin16(nSLD),
    .pin18(1'b0), .pin19(1'b0), .pin20(OP3), .pin21(OP2), .pin22(OP1), .pin23(OP0), .pin24(1'b1));  // open: pin1, pin17
  // Probe on mon_sft_unit
  // Probe on mon_math_unit
  _7408 _4x2xAND (
    .pin1(nADD), .pin2(nADDI), .pin3(nADDs), .pin4(nSUB), .pin5(nSUBI), .pin6(nBOR), .pin7(1'b0),
    .pin8(nORs), .pin9(nORI), .pin10(nOR), .pin11(nANDs), .pin12(nANDI), .pin13(nAND), .pin14(1'b1));

  // Other names for the same wires on the sheet: nSUBs = nBOR

  // Notes on the sheet:
  //   nCLR: default 1
  //   Part of 
  //   Math Unit 7404
  //   Math Mode Encoder
  //   Y0 ADD
  //   Y1 SUB
  //   Y2 ADDI
  //   Y3 SUBI
  //   Y4 AND
  //   Y5 OR
  //   Y6 XOR
  //   Y7 ANDI
  //   Y8 ORI
  //   Y9 SLL
  //   Y10 SRL
  //   Y11 ROL
  //   Y12 ROR
  //   Y13 SLD
  //   ADD && ADDI
  //   SUB && SUBI
  //   AND && ANDI
  //   OR && ORI
endmodule
