// Digital circuit Branch.dig as structural Verilog
module Branch (
  input  Z,
  input  C,
  input  CTRL0,
  input  CTRL1,
  input  CTRL2,
  output njmp
);

  wire _7486_1_pin6, _74153_1_pin7;

  _74153 _74153_1 (
    .pin1(1'b0), .pin2(CTRL1), .pin3(1'b0), .pin4(Z), .pin5(C), .pin6(1'b0), .pin7(_74153_1_pin7),
    .pin8(1'b0), .pin10(1'b0), .pin11(1'b0), .pin12(1'b0), .pin13(1'b0), .pin14(CTRL0), .pin15(1'b1),
    .pin16(1'b1));  // open: pin9
  _7486 _7486_1 (
    .pin1(1'b0), .pin2(1'b0), .pin4(_74153_1_pin7), .pin5(CTRL2), .pin6(_7486_1_pin6), .pin7(1'b0),
    .pin9(1'b0), .pin10(1'b0), .pin12(1'b0), .pin13(1'b0), .pin14(1'b1));  // open: pin3, pin8, pin11
  _7404 _7404_1 (
    .pin1(1'b0), .pin3(1'b0), .pin5(_7486_1_pin6), .pin6(njmp), .pin7(1'b0), .pin9(1'b0), .pin11(1'b0),
    .pin13(1'b0), .pin14(1'b1));  // open: pin2, pin4, pin8, pin10, pin12

  // Notes on the sheet:
  //   Branch Control Logic
  //   C2 C1 C0 Operation
  //   0    0    0    Noop
  //   0    0    1    Branch if Carry (C)
  //   0    1    0    Branch if Zero (Z)
  //   1    x    x    Jump (J)
endmodule
