// Digital circuit Comparator-Unit.dig as structural Verilog
module Comparator_Unit (
  input  A0,
  input  A1,
  input  A2,
  input  A3,
  input  A4,
  input  A5,
  input  A6,
  input  A7,
  input  A8,
  input  A9,
  input  A10,
  input  A11,
  input  A12,
  input  A13,
  input  A14,
  input  A15,
  output Zero
);

  wire _7404_1_pin6, _7404_1_pin8, _7404_1_pin9, LO_pin19;
  wire [3:3] X2_0_3;

  _74688 LO (
    .pin1(1'b0), .pin2(A0), .pin3(X2_0_3[3]), .pin4(A1), .pin5(X2_0_3[3]), .pin6(A2), .pin7(X2_0_3[3]),
    .pin8(A3), .pin9(X2_0_3[3]), .pin10(1'b0), .pin11(A4), .pin12(X2_0_3[3]), .pin13(A5), .pin14(X2_0_3[3]),
    .pin15(A6), .pin16(X2_0_3[3]), .pin17(A7), .pin18(X2_0_3[3]), .pin19(LO_pin19), .pin20(1'b1));
  _7404 _7404_1 (
    .pin1(1'b0), .pin3(1'b0), .pin5(LO_pin19), .pin6(_7404_1_pin6), .pin7(1'b0), .pin8(_7404_1_pin8),
    .pin9(_7404_1_pin9), .pin11(1'b0), .pin13(1'b0), .pin14(1'b1));  // open: pin2, pin4, pin10, pin12
  _74688 HI (
    .pin1(1'b0), .pin2(A8), .pin3(X2_0_3[3]), .pin4(A9), .pin5(X2_0_3[3]), .pin6(A10), .pin7(X2_0_3[3]),
    .pin8(A11), .pin9(X2_0_3[3]), .pin10(1'b0), .pin11(A12), .pin12(X2_0_3[3]), .pin13(A13),
    .pin14(X2_0_3[3]), .pin15(A14), .pin16(X2_0_3[3]), .pin17(A15), .pin18(X2_0_3[3]), .pin19(_7404_1_pin9),
    .pin20(1'b1));
  _7408 _7408_1 (
    .pin1(_7404_1_pin6), .pin2(_7404_1_pin8), .pin3(Zero), .pin4(1'b0), .pin5(1'b0), .pin7(1'b0),
    .pin9(1'b0), .pin10(1'b0), .pin12(1'b0), .pin13(1'b0), .pin14(1'b1));  // open: pin6, pin8, pin11
  // also tied to GND on the sheet: X2_0_3[3]

  // Other names for the same wires on the sheet: X2_0_3[2:0] = {3{X2_0_3[3]}}; X2_4_7[3:0] = {4{X2_0_3[3]}};
  //   X2_8_11[3:0] = {4{X2_0_3[3]}}; X2_12_15[3:0] = {4{X2_0_3[3]}}; X1_0_3[3:0] = {A3, A2, A1, A0};
  //   X1_4_7[3:0] = {A7, A6, A5, A4}; X1_8_11[3:0] = {A11, A10, A9, A8}; X1_12_15[3:0] = {A15, A14, A13, A12}
endmodule
