// Digital circuit Decoder.dig as structural Verilog
module Decoder (
  input  nOE,
  input  nCE,
  input  nWE,
  input  Rdest0,
  input  Rdest1,
  input  Rdest2,
  input  Rdest3,
  input  Rsrc0,
  input  Rsrc1,
  input  Rsrc2,
  input  Rsrc3,
  input  OP0,
  input  OP1,
  input  OP2,
  input  OP3,
  input  OP4,
  input  OP5,
  input  OP6,
  input  OP7,
  output [31:0] D
);

  wire _2cyc, _74244_2_p6, immOE, memOE, memWE, not_1_out, nrdWE, nrs0WE, nrs1WE, nrs2WE, nrs3WE;
  wire [7:0] A;

  // _28c256 DEC_ROM0: pin names not known; wires that end beside it: 1'b0, 1'b0, A[7], A[6], A[5], A[4], A[3], A[2], A[1], A[0], D[10], D[1], D[2], 1'b0, 1'b1, nWE, 1'b0, 1'b0, 1'b0, 1'b0, nOE, 1'b0, nCE, D[7]
  // _28c256 DEC_ROM1: pin names not known; wires that end beside it: 1'b0, 1'b0, A[7], A[6], A[5], A[4], A[3], A[2], A[1], A[0], D[8], D[9], D[10], 1'b0, 1'b1, nWE, 1'b0, 1'b0, 1'b0, 1'b0, nOE, 1'b0, nCE, D[15]
  _7432 _7432_1 (
    .pin1(D[10]), .pin2(D[9]), .pin3(_2cyc), .pin4(1'b0), .pin5(1'b0), .pin7(1'b0), .pin9(1'b0),
    .pin10(1'b0), .pin12(1'b0), .pin13(1'b0), .pin14(1'b1));  // open: pin6, pin8, pin11
  // _28c256 DEC_ROM2: pin names not known; wires that end beside it: 1'b0, 1'b0, A[7], A[6], A[5], A[4], A[3], A[2], A[1], A[0], D[16], D[17], D[18], 1'b0, 1'b1, nWE, 1'b0, 1'b0, 1'b0, 1'b0, nOE, 1'b0, nCE, D[23]
  not not_1 (not_1_out, _2cyc);
  // _74244 _74244_1: pin names not known; wires that end beside it: _2cyc, OP0, OP1, OP2, OP3, not_1_out, 1'b0, 1'b0, 1'b0, 1'b0, 1'b1, 1'b0, A[0], A[1], A[2], A[3], A[0], A[1], A[2], A[3]
  _74138 _74138_1 (
    .pin1(Rdest0), .pin2(Rdest1), .pin3(Rdest2), .pin4(1'b0), .pin5(1'b0), .pin6(1'b1), .pin8(1'b0),
    .pin10(nrs3WE), .pin11(nrs2WE), .pin12(nrdWE), .pin13(nrs1WE), .pin14(nrs0WE), .pin16(1'b1));  // open: pin7, pin9, pin15
  _7404 _7404_1 (
    .pin1(nrs0WE), .pin2(D[24]), .pin3(nrs1WE), .pin4(D[25]), .pin5(nrdWE), .pin6(D[26]), .pin7(1'b0),
    .pin9(1'b0), .pin10(D[28]), .pin11(nrs3WE), .pin12(D[27]), .pin13(nrs2WE), .pin14(1'b1));  // open: pin8
  // _74244 _74244_2: pin names not known; wires that end beside it: _2cyc, OP4, OP5, OP6, OP7, _74244_2_p6, 1'b0, 1'b0, 1'b0, 1'b0, 1'b1, 1'b0, A[4], A[5], A[6], A[7], A[4], A[5], A[6], A[7]
  not not_2 (_74244_2_p6, _2cyc);
  _74138 _74138_2 (
    .pin1(Rsrc0), .pin2(Rsrc1), .pin3(Rsrc2), .pin4(1'b0), .pin5(1'b0), .pin6(1'b1), .pin8(1'b0),
    .pin12(D[31]), .pin13(D[30]), .pin14(D[29]), .pin16(1'b1));  // open: pin7, pin9, pin10, pin11, pin15
  _7404 _7404_2 (
    .pin1(1'b0), .pin3(1'b0), .pin5(memWE), .pin6(D[4]), .pin7(1'b0), .pin8(D[5]), .pin9(immOE),
    .pin10(D[3]), .pin11(memOE), .pin13(1'b0), .pin14(1'b1));  // open: pin2, pin4, pin12

  assign D[0] = D[10];

  // Other names for the same wires on the sheet: D0[7:0] = {D[7:1], D[10]}; D1[7:0] = D[15:8]; imm = D[10];
  //   imem = D[1]; outEN = D[2]; D2[7:0] = D[23:16]; AL[3:0] = A[3:0]; AH[3:0] = A[7:4]; nimmOE = D[5]; nmemOE = D[3];
  //   nmemWE = D[4]; nrdOE = D[29]; nrs2OE = D[30]; nrs3OE = D[31]; opl[3:0] = {OP3, OP2, OP1, OP0};
  //   oph[3:0] = {OP7, OP6, OP5, OP4}; pmem = D[9]; rdWE = D[26]; rs0WE = D[24]; rs1WE = D[25]; rs2WE = D[27];
  //   rs3WE = D[28]

  // Notes on the sheet:
  //   nWE: default 1
  //   I/O
  //   Decoder ROMs
  //   Inputs
  //   Outputs
  //   Register Address Decoder
  //   Force nop if imm OR pmem is set
  //   contents of DEC-ROM0 (hex, n*v repeats v):
  //   8*0,13,14,18
endmodule
