// Digital circuit Decoder_v2.dig as structural Verilog
module Decoder_v2 (
  input  [7:0] Op,
  input  nOE,
  input  nCE,
  input  nWE,
  input  IMM,
  output [23:0] D
);

  wire _74244_1_p6, not_2_out;
  wire [7:0] A;

  // _28c256 DEC_ROM0: pin names not known; wires that end beside it: 1'b0, 1'b0, A[7], A[6], A[5], A[4], A[3], A[2], A[1], A[0], D[0], D[1], D[2], 1'b0, 1'b1, nWE, 1'b0, 1'b0, 1'b0, 1'b0, nOE, 1'b0, nCE, D[7]
  // _28c256 DEC_ROM1: pin names not known; wires that end beside it: 1'b0, 1'b0, A[7], A[6], A[5], A[4], A[3], A[2], A[1], A[0], D[8], D[9], D[10], 1'b0, 1'b1, nWE, 1'b0, 1'b0, 1'b0, 1'b0, nOE, 1'b0, nCE, D[15]
  // _74244 _74244_1: pin names not known; wires that end beside it: IMM, Op[0], Op[1], Op[2], Op[3], _74244_1_p6, 1'b0, 1'b0, 1'b0, 1'b0, 1'b1, 1'b0, A[0], A[1], A[2], A[3], A[0], A[1], A[2], A[3]
  not not_1 (_74244_1_p6, IMM);
  not not_2 (not_2_out, IMM);
  // _74244 _74244_2: pin names not known; wires that end beside it: IMM, Op[4], Op[5], Op[6], Op[7], not_2_out, 1'b0, 1'b0, 1'b0, 1'b0, 1'b1, 1'b0, A[4], A[5], A[6], A[7], A[4], A[5], A[6], A[7]

  // Other names for the same wires on the sheet: D0[7:0] = D[7:0]; D1[7:0] = D[15:8]; AL[3:0] = A[3:0];
  //   AH[3:0] = A[7:4]; D2[7:0] = D[23:16]; opl[3:0] = Op[3:0]; oph[3:0] = Op[7:4]

  // Notes on the sheet:
  //   nWE: default 1
  //   I/O
  //   Decoder ROMs
  //   Inputs
  //   Outputs
  //   Force nop if imm is set
endmodule
