// Digital circuit Display_Decoder.dig as structural Verilog
module Display_Decoder (
  input  CLK,
  input  nCLR,
  input  EN,
  input  D0,
  input  D1,
  input  D2,
  input  D3,
  input  D4,
  input  D5,
  input  D6,
  input  D7,
  input  D8,
  input  D9,
  input  D10,
  input  D11,
  input  D12,
  input  D13,
  input  D14,
  input  D15,
  output a0,
  output b0,
  output c0,
  output d0_2,
  output e0,
  output f0,
  output g0,
  output a1,
  output b1,
  output c1,
  output d1_2,
  output e1,
  output f1,
  output g1,
  output a2,
  output b2,
  output c2,
  output d2_2,
  output e2,
  output f2,
  output g2,
  output a3,
  output b3,
  output c3,
  output d3_2,
  output e3,
  output f3,
  output g3
);

  wire _16_bit_register_1_q0, _16_bit_register_1_q1, _16_bit_register_1_q2, _16_bit_register_1_q3,
       _16_bit_register_1_q4, _16_bit_register_1_q5, _16_bit_register_1_q6, _16_bit_register_1_q7,
       _16_bit_register_1_q8, _16_bit_register_1_q9, _16_bit_register_1_q10, _16_bit_register_1_q11,
       _16_bit_register_1_q12, _16_bit_register_1_q13, _16_bit_register_1_q14, _16_bit_register_1_q15;

  _16_Bit_Register _16_bit_register_1 (
    .D0(D0), .D1(D1), .D2(D2), .D3(D3), .D4(D4), .D5(D5), .D6(D6), .D7(D7), .D8(D8), .D9(D9), .D10(D10),
    .D11(D11), .D12(D12), .D13(D13), .D14(D14), .D15(D15), .EN(EN), .CLK(CLK), .nCLR(nCLR),
    .Q0(_16_bit_register_1_q0), .Q1(_16_bit_register_1_q1), .Q2(_16_bit_register_1_q2),
    .Q3(_16_bit_register_1_q3), .Q4(_16_bit_register_1_q4), .Q5(_16_bit_register_1_q5),
    .Q6(_16_bit_register_1_q6), .Q7(_16_bit_register_1_q7), .Q8(_16_bit_register_1_q8),
    .Q9(_16_bit_register_1_q9), .Q10(_16_bit_register_1_q10), .Q11(_16_bit_register_1_q11),
    .Q12(_16_bit_register_1_q12), .Q13(_16_bit_register_1_q13), .Q14(_16_bit_register_1_q14),
    .Q15(_16_bit_register_1_q15));
  // _28c16 ROM3: pin names not known; wires that end beside it: 1'b0, 1'b0, 1'b0, 1'b0, _16_bit_register_1_q15, _16_bit_register_1_q14, _16_bit_register_1_q13, _16_bit_register_1_q12, a3, b3, c3, 1'b0, 1'b1, 1'b0, 1'b0, 1'b1, 1'b0, 1'b0, 1'b0, g3, f3
  // _28c16 ROM2: pin names not known; wires that end beside it: 1'b0, 1'b0, 1'b0, 1'b0, _16_bit_register_1_q11, _16_bit_register_1_q10, _16_bit_register_1_q9, _16_bit_register_1_q8, a2, b2, c2, 1'b0, 1'b1, 1'b0, 1'b0, 1'b1, 1'b0, 1'b0, 1'b0, g2, f2
  // _28c16 ROM1: pin names not known; wires that end beside it: 1'b0, 1'b0, 1'b0, 1'b0, _16_bit_register_1_q7, _16_bit_register_1_q6, _16_bit_register_1_q5, _16_bit_register_1_q4, a1, b1, c1, 1'b0, 1'b1, 1'b0, 1'b0, 1'b1, 1'b0, 1'b0, 1'b0, g1, f1
  // _28c16 ROM0: pin names not known; wires that end beside it: 1'b0, 1'b0, 1'b0, 1'b0, _16_bit_register_1_q3, _16_bit_register_1_q2, _16_bit_register_1_q1, _16_bit_register_1_q0, a0, b0, c0, 1'b0, 1'b1, 1'b0, 1'b0, 1'b1, 1'b0, 1'b0, 1'b0, g0, f0

  // Notes on the sheet:
  //   nCLR: default 1
  //   EN: default 1
endmodule
