// Digital circuit Display_Decoder_v2.dig as structural Verilog
module Display_Decoder_v2 (
  input  D15,
  input  D14,
  input  D13,
  input  D12,
  input  D11,
  input  D10,
  input  D9,
  input  D8,
  input  D7,
  input  D6,
  input  D5,
  input  D4,
  input  D3,
  input  D2,
  input  D1,
  input  D0,
  input  WE,
  input  nCLR,
  input  CLK,
  input  OUT_CLK,
  output g,
  output f,
  output e,
  output d,
  output c,
  output b,
  output a,
  output dig1,
  output dig2,
  output dig3,
  output dig4
);

  wire _74253_1_pin2, _74253_1_pin7, _74253_1_pin9, _74253_1_pin14, _74253_2_pin7, _74253_2_pin9, Q0, Q1, Q2,
       Q3, Q4, Q5, Q6, Q7, Q8, Q9, Q10, Q11, Q12, Q13, Q14, Q15;

  _16_Bit_Register _16_bit_register_1 (
    .D0(D0), .D1(D1), .D2(D2), .D3(D3), .D4(D4), .D5(D5), .D6(D6), .D7(D7), .D8(D8), .D9(D9), .D10(D10),
    .D11(D11), .D12(D12), .D13(D13), .D14(D14), .D15(D15), .EN(WE), .CLK(CLK), .nCLR(nCLR), .Q0(Q0), .Q1(Q1),
    .Q2(Q2), .Q3(Q3), .Q4(Q4), .Q5(Q5), .Q6(Q6), .Q7(Q7), .Q8(Q8), .Q9(Q9), .Q10(Q10), .Q11(Q11), .Q12(Q12),
    .Q13(Q13), .Q14(Q14), .Q15(Q15));
  _74253 _74253_1 (
    .pin1(1'b0), .pin2(_74253_1_pin2), .pin3(Q12), .pin4(Q8), .pin5(Q4), .pin6(Q0), .pin7(_74253_1_pin7),
    .pin8(1'b0), .pin9(_74253_1_pin9), .pin10(Q1), .pin11(Q5), .pin12(Q9), .pin13(Q13),
    .pin14(_74253_1_pin14), .pin15(1'b0), .pin16(1'b1));
  _74253 _74253_2 (
    .pin1(1'b0), .pin2(_74253_1_pin2), .pin3(Q14), .pin4(Q10), .pin5(Q6), .pin6(Q2), .pin7(_74253_2_pin7),
    .pin8(1'b0), .pin9(_74253_2_pin9), .pin10(Q3), .pin11(Q7), .pin12(Q11), .pin13(Q15),
    .pin14(_74253_1_pin14), .pin15(1'b0), .pin16(1'b1));
  _74161 _74161_1 (
    .pin1(1'b1), .pin2(OUT_CLK), .pin3(1'b0), .pin4(1'b0), .pin5(1'b0), .pin6(1'b0), .pin7(1'b1),
    .pin8(1'b0), .pin9(1'b1), .pin10(1'b1), .pin13(_74253_1_pin14), .pin14(_74253_1_pin2), .pin16(1'b1));  // open: pin11, pin12, pin15
  // _28c16 OUT_ROM: pin names not known; wires that end beside it: 1'b1, 1'b0, 1'b0, 1'b0, 1'b0, 1'b0, 1'b1, 1'b0, 1'b0, _74253_2_pin9, 1'b0, _74253_2_pin7, 1'b0, _74253_1_pin9, _74253_1_pin7, g, a, f, b, c, 1'b0
  Seven_Seg #(.commonCathode("true")) seven_seg_1 (
    .a(a), .b(b), .c(c), .d(d), .e(e), .f(f), .g(g), .dp(1'b0), .common(dig1));
  _74139 _74139_1 (
    .pin1(1'b0), .pin2(_74253_1_pin2), .pin3(_74253_1_pin14), .pin4(dig4), .pin5(dig3), .pin6(dig2),
    .pin7(dig1), .pin8(1'b0), .pin13(1'b0), .pin14(1'b0), .pin15(1'b1), .pin16(1'b1));  // open: pin9, pin10, pin11, pin12
  Seven_Seg #(.commonCathode("true")) seven_seg_2 (
    .a(a), .b(b), .c(c), .d(d), .e(e), .f(f), .g(g), .dp(1'b0), .common(dig2));
  Seven_Seg #(.commonCathode("true")) seven_seg_3 (
    .a(a), .b(b), .c(c), .d(d), .e(e), .f(f), .g(g), .dp(1'b0), .common(dig3));
  Seven_Seg #(.commonCathode("true")) seven_seg_4 (
    .a(a), .b(b), .c(c), .d(d), .e(e), .f(f), .g(g), .dp(1'b0), .common(dig4));

  // Notes on the sheet:
  //   CLK: Hz: 30
  //   OUT_CLK: Hz: 20
  //   contents of OUT-ROM (hex, n*v repeats v):
  //   3f,6,5b,4f,66,6d,7d,7,7f,6f,77,7c,39,5e,79,71
endmodule
