// Digital circuit Flags_Register.dig as structural Verilog
module Flags_Register (
  input  Ci,
  input  Zi,
  input  CLK,
  input  nCLR,
  input  store,
  output Zo,
  output Co
);

  wire _74273_1_pin11;

  _74273 _74273_1 (
    .pin1(nCLR), .pin2(Co), .pin3(Ci), .pin4(1'b0), .pin6(Zo), .pin7(Zi), .pin8(1'b0), .pin10(1'b0),
    .pin11(_74273_1_pin11), .pin13(1'b0), .pin14(1'b0), .pin17(1'b0), .pin18(1'b0), .pin20(1'b1));  // open: pin5, pin9, pin12, pin15, pin16, pin19
  _7408 _7408_1 (
    .pin1(CLK), .pin2(store), .pin3(_74273_1_pin11), .pin4(1'b0), .pin5(1'b0), .pin7(1'b0), .pin9(1'b0),
    .pin10(1'b0), .pin12(1'b0), .pin13(1'b0), .pin14(1'b1));  // open: pin6, pin8, pin11

  // Other names for the same wires on the sheet: EN = store

  // Notes on the sheet:
  //   nCLR: default 1
  //   store: default 1
  //   Inputs
  //   Outputs
endmodule
