# Fritzing sketch Bottom_Layer (saved by Fritzing 0.9.9b)
breadboards: 12

parts:
  Breadboard11 = Breadboard Split Power  # not connected
  Breadboard12 = Breadboard Split Power  # not connected
  Breadboard13 = Breadboard Split Power  # not connected
  Breadboard14 = Breadboard Split Power  # not connected
  Breadboard15 = Breadboard Split Power  # not connected
  Breadboard16 = Breadboard Split Power  # not connected
  Breadboard17 = Breadboard Split Power  # not connected
  Breadboard18 = Breadboard Split Power  # not connected
  Breadboard19 = Breadboard Split Power  # not connected
  Breadboard20 = Breadboard Split Power  # not connected
  Breadboard21 = Breadboard Split Power  # not connected
  Breadboard22 = Breadboard Split Power  # not connected
  Breadboard23 = Breadboard Split Power  # not connected
  Breadboard24 = Breadboard Split Power  # not connected
  Breadboard25 = Breadboard Split Power  # not connected
  Breadboard26 = Breadboard Split Power  # not connected
  Breadboard27 = Breadboard Split Power  # not connected
  Breadboard28 = Breadboard Split Power  # not connected
  Breadboard29 = Breadboard Split Power  # not connected
  Breadboard30 = Breadboard Split Power  # not connected
  Breadboard31 = Breadboard Split Power  # not connected
  Breadboard32 = Breadboard Split Power  # not connected
  Breadboard33 = Breadboard Split Power  # not connected
  Breadboard34 = Breadboard Split Power  # not connected
  Breadboard62 = Breadboard Split Power  # not connected
  Breadboard63 = Breadboard Split Power  # not connected
  Breadboard64 = Breadboard Split Power  # not connected
  Breadboard65 = Breadboard Split Power  # not connected
  Breadboard66 = Breadboard Split Power  # not connected
  Breadboard67 = Breadboard Split Power  # not connected
  Breadboard68 = Breadboard Split Power  # not connected
  Breadboard69 = Breadboard Split Power  # not connected
  IC14 = IC, DIP package, 20 pins [chip_label=74273]  # not connected
  IC15 = IC, DIP package, 20 pins [chip_label=74273]  # not connected
  IC16 = IC, DIP package, 14 pins [chip_label=7408]  # not connected
  IC17 = IC, DIP package, 20 pins [chip_label="74245 Driver"]  # not connected
  IC18 = IC, DIP package, 20 pins [chip_label="74245 Driver"]  # not connected
  IC47 = IC, DIP package, 24 pins [chip_label="HM6116 RAM"]  # not connected
  IC48 = IC, DIP package, 24 pins [chip_label="HM6116 RAM"]
  IC49 = IC, DIP package, 20 pins [chip_label=74273]  # not connected
  IC50 = IC, DIP package, 20 pins [chip_label=74273]  # not connected
  IC51 = IC, DIP package, 14 pins [chip_label=7408]  # not connected
  IC52 = IC, DIP package, 14 pins [chip_label="7432 OR"]  # not connected
  Breadboard75 = Breadboard Split Power  # not connected
  Breadboard76 = Breadboard Split Power  # not connected
  Breadboard77 = Breadboard Split Power  # not connected
  Breadboard78 = Breadboard Split Power  # not connected
  Breadboard79 = Breadboard Split Power  # not connected
  Breadboard80 = Breadboard Split Power  # not connected
  Breadboard81 = Breadboard Split Power  # not connected
  Breadboard82 = Breadboard Split Power  # not connected
  IC57 = IC, DIP package, 20 pins [chip_label="74245 Driver"]  # not connected
  IC58 = IC, DIP package, 20 pins [chip_label="74245 Driver"]  # not connected
  IC61 = IC, DIP package, 24 pins [chip_label="HM6116 RAM"]
  IC64 = IC, DIP package, 20 pins [chip_label="74245 Driver"]  # not connected
  IC65 = IC, DIP package, 20 pins [chip_label=74273]  # not connected
  IC66 = IC, DIP package, 20 pins [chip_label=74273]  # not connected
  IC68 = IC, DIP package, 20 pins [chip_label="74245 Driver"]  # not connected
  IC69 = IC, DIP package, 28 pins [chip_label=28c256]  # not connected
  IC70 = IC, DIP package, 28 pins [chip_label=28c256]  # not connected
  IC71 = IC, DIP package, 20 pins [chip_label=74245]  # not connected
  IC72 = IC, DIP package, 20 pins [chip_label=74245]  # not connected
  Part1 = Breadboard Power Supply Board SMD  # not connected
  S1 = Momentary Switch [package=ksa_sealed_tac_switch]  # not connected
  SW1 = DIP SWITCH [package=dipswitch-02]  # not connected
  SW2 = DIP SWITCH [package=dipswitch-02]  # not connected
  IC73 = IC, DIP package, 24 pins [chip_label=24C16]  # not connected
  LED1 = LED - 5mm [color="Red (633nm)" current=0.030 package="5 mm [THT]"]  # not connected
  LED2 = LED - 5mm [color="Red (633nm)" current=0.030 package="5 mm [THT]"]  # not connected
  LED3 = LED - 5mm [color="Red (633nm)" current=0.030 package="5 mm [THT]"]  # not connected
  LED4 = LED - 5mm [color="Red (633nm)" current=0.030 package="5 mm [THT]"]  # not connected
  LED5 = LED - 5mm [color="Red (633nm)" current=0.030 package="5 mm [THT]"]  # not connected
  LED6 = LED - 5mm [color="Red (633nm)" current=0.030 package="5 mm [THT]"]  # not connected
  LED7 = LED - 5mm [color="Red (633nm)" current=0.030 package="5 mm [THT]"]  # not connected
  LED8 = LED - 5mm [color="Red (633nm)" current=0.030 package="5 mm [THT]"]  # not connected
  IC74 = IC, DIP package, 16 pins [chip_label=74138]  # not connected
  IC75 = IC, DIP package, 16 pins [chip_label=74138]  # not connected
  IC76 = IC, DIP package, 28 pins [chip_label=28c256]  # not connected
  IC77 = IC, DIP package, 14 pins [chip_label=7404]  # not connected

nets:
  N1: IC48.pin1, IC61.pin1
  N2: IC48.pin2, IC61.pin2
  N3: IC48.pin3, IC61.pin3
  N4: IC48.pin4, IC61.pin4
  N5: IC48.pin5, IC61.pin5
  N6: IC48.pin6, IC61.pin6
  N7: IC48.pin7, IC61.pin7
  N8: IC48.pin8, IC61.pin8
  N9: IC48.pin9, IC61.pin9
  N10: IC48.pin10, IC61.pin10
  N11: IC48.pin11, IC61.pin11
  N12: IC48.pin12, IC61.pin12
  N13: IC48.pin13, IC61.pin13
  N14: IC48.pin14, IC61.pin14
  N15: IC48.pin15, IC61.pin15
  N16: IC48.pin16, IC61.pin16
  N17: IC48.pin17, IC61.pin17
  N18: IC48.pin18, IC61.pin18
  N19: IC48.pin19, IC61.pin19
  N20: IC48.pin20, IC61.pin20
  N21: IC48.pin21, IC61.pin21
  N22: IC48.pin22, IC61.pin22
  N23: IC48.pin23, IC61.pin23
  N24: IC48.pin24, IC61.pin24

notes:
  Bottom Layer
  General Purpose Registers (rs2, rs3)
  RAM
  16-Bit BUS
  16-Bit BUS Interfaces
  Clock & Power Interfaces
  rs3 register
  ImRegister
  16-Bit Breadboard Processor
  BUS
  >BUS
  Decoder Interfaces
  INST BUS
  INST
  Instruction Register
  Instruction Bus
  EEPROM Programmer
  INST BUS Interfaces
  <BUS
  rs2 register
  Decoder ROMs
  Instruction Decoder
  Register Decoder
  Shared 7408

custom parts:
  Breadboard Split Power: A custom 6 pin per group power supply strip where the top row (ground) is all bussed together and the bottom row (+V) is split in two groups of 12 pins. This version is modified to be a loadable part and was rescaled to be on the standard 1px = 1thou grid with the size set in inches
