# Fritzing sketch Middle_Layer (saved by Fritzing 0.9.9b)
breadboards: 12

parts:
  Breadboard11 = Breadboard Split Power  # not connected
  Breadboard12 = Breadboard Split Power  # not connected
  Breadboard13 = Breadboard Split Power  # not connected
  Breadboard14 = Breadboard Split Power  # not connected
  Breadboard15 = Breadboard Split Power  # not connected
  Breadboard16 = Breadboard Split Power  # not connected
  Breadboard17 = Breadboard Split Power  # not connected
  Breadboard18 = Breadboard Split Power  # not connected
  Breadboard19 = Breadboard Split Power  # not connected
  Breadboard20 = Breadboard Split Power  # not connected
  Breadboard21 = Breadboard Split Power  # not connected
  Breadboard22 = Breadboard Split Power  # not connected
  Breadboard23 = Breadboard Split Power  # not connected
  Breadboard24 = Breadboard Split Power  # not connected
  Breadboard25 = Breadboard Split Power  # not connected
  Breadboard26 = Breadboard Split Power  # not connected
  Breadboard27 = Breadboard Split Power  # not connected
  Breadboard28 = Breadboard Split Power  # not connected
  Breadboard29 = Breadboard Split Power  # not connected
  Breadboard30 = Breadboard Split Power  # not connected
  Breadboard31 = Breadboard Split Power  # not connected
  Breadboard32 = Breadboard Split Power  # not connected
  Breadboard33 = Breadboard Split Power  # not connected
  Breadboard34 = Breadboard Split Power  # not connected
  Breadboard62 = Breadboard Split Power  # not connected
  Breadboard63 = Breadboard Split Power  # not connected
  Breadboard64 = Breadboard Split Power  # not connected
  Breadboard65 = Breadboard Split Power  # not connected
  Breadboard66 = Breadboard Split Power  # not connected
  Breadboard67 = Breadboard Split Power  # not connected
  Breadboard68 = Breadboard Split Power  # not connected
  Breadboard69 = Breadboard Split Power  # not connected
  IC8 = IC, DIP package, 20 pins [chip_label=74273]  # not connected
  IC9 = IC, DIP package, 20 pins [chip_label=74273]  # not connected
  IC11 = IC, DIP package, 20 pins [chip_label=74273]  # not connected
  IC12 = IC, DIP package, 20 pins [chip_label=74273]  # not connected
  IC13 = IC, DIP package, 14 pins [chip_label=7408]  # not connected
  IC21 = IC, DIP package, 20 pins [chip_label=74382]  # not connected
  IC22 = IC, DIP package, 20 pins [chip_label=74382]  # not connected
  IC23 = IC, DIP package, 20 pins [chip_label=74382]  # not connected
  IC24 = IC, DIP package, 20 pins [chip_label=74382]  # not connected
  IC25 = IC, DIP package, 14 pins [chip_label="7432 OR"]  # not connected
  IC26 = IC, DIP package, 24 pins [chip_label="74154 4-to-16 Encode"]  # not connected
  IC29 = IC, DIP package, 16 pins [chip_label="74148 8-3 Pri Enc"]  # not connected
  IC32 = IC, DIP package, 20 pins [chip_label="74299 Shift"]
  IC33 = IC, DIP package, 20 pins [chip_label="74299 Shift"]
  IC36 = IC, DIP package, 14 pins [chip_label=7408]  # not connected
  IC38 = IC, DIP package, 16 pins [chip_label="74148 8-3 Pri Enc"]  # not connected
  IC39 = IC, DIP package, 20 pins [chip_label="74688 Compare"]
  IC40 = IC, DIP package, 20 pins [chip_label="74688 Compare"]
  IC41 = IC, DIP package, 14 pins [chip_label="7404 NOT"]  # not connected
  IC42 = IC, DIP package, 14 pins [chip_label="7408 AND"]  # not connected
  IC55 = IC, DIP package, 20 pins [chip_label="74273 Register"]  # not connected
  IC45 = IC, DIP package, 14 pins [chip_label="7404 NOT"]  # not connected
  IC46 = IC, DIP package, 14 pins [chip_label="7400 NAND"]  # not connected
  Breadboard75 = Breadboard Split Power  # not connected
  Breadboard76 = Breadboard Split Power  # not connected
  Breadboard77 = Breadboard Split Power  # not connected
  Breadboard78 = Breadboard Split Power  # not connected
  Breadboard79 = Breadboard Split Power  # not connected
  Breadboard80 = Breadboard Split Power  # not connected
  Breadboard81 = Breadboard Split Power  # not connected
  Breadboard82 = Breadboard Split Power  # not connected
  IC59 = IC, DIP package, 20 pins [chip_label=74688]
  IC60 = IC, DIP package, 20 pins [chip_label=74688]
  IC63 = IC, DIP package, 20 pins [chip_label=74245]  # not connected
  IC64 = IC, DIP package, 20 pins [chip_label=74245]  # not connected
  IC67 = IC, DIP package, 20 pins [chip_label=74299]
  IC68 = IC, DIP package, 20 pins [chip_label=74299]
  IC69 = IC, DIP package, 20 pins [chip_label="74245 Driver"]  # not connected
  IC70 = IC, DIP package, 20 pins [chip_label="74245 Driver"]  # not connected
  IC73 = IC, DIP package, 14 pins [chip_label=7408]  # not connected
  IC74 = IC, DIP package, 20 pins [chip_label="74245 Driver"]  # not connected
  IC75 = IC, DIP package, 20 pins [chip_label="74245 Driver"]  # not connected
  IC76 = IC, DIP package, 14 pins [chip_label=7408]  # not connected
  IC77 = IC, DIP package, 20 pins [chip_label=74273]  # not connected
  IC78 = IC, DIP package, 14 pins [chip_label=7408]  # not connected
  IC79 = IC, DIP package, 20 pins [chip_label=74273]  # not connected
  IC80 = IC, DIP package, 20 pins [chip_label="74245 Driver"]  # not connected
  IC81 = IC, DIP package, 20 pins [chip_label="74245 Driver"]  # not connected
  IC83 = IC, DIP package, 14 pins [chip_label="7486 XOR"]  # not connected
  IC84 = IC, DIP package, 16 pins [chip_label=74153]  # not connected

nets:
  N1: IC32.pin3, IC67.pin1
  N2: IC32.pin4, IC67.pin2
  N3: IC32.pin5, IC67.pin3
  N4: IC32.pin6, IC67.pin4
  N5: IC32.pin7, IC67.pin5
  N6: IC32.pin8, IC67.pin6
  N7: IC32.pin9, IC67.pin7
  N8: IC32.pin10, IC67.pin8
  N9: IC32.pin11, IC67.pin13
  N10: IC32.pin12, IC67.pin14
  N11: IC32.pin13, IC67.pin15
  N12: IC32.pin14, IC67.pin16
  N13: IC32.pin15, IC67.pin17
  N14: IC32.pin16, IC67.pin18
  N15: IC32.pin17, IC67.pin19
  N16: IC32.pin18, IC67.pin20
  N17: IC33.pin1, IC68.pin1
  N18: IC33.pin2, IC68.pin2
  N19: IC33.pin3, IC68.pin3
  N20: IC33.pin4, IC68.pin4
  N21: IC33.pin5, IC68.pin5
  N22: IC33.pin6, IC68.pin6
  N23: IC33.pin7, IC68.pin7
  N24: IC33.pin8, IC68.pin8
  N25: IC33.pin9, IC68.pin9
  N26: IC33.pin10, IC68.pin10
  N27: IC33.pin11, IC68.pin11
  N28: IC33.pin12, IC68.pin12
  N29: IC33.pin13, IC68.pin13
  N30: IC33.pin14, IC68.pin14
  N31: IC33.pin15, IC68.pin15
  N32: IC33.pin16, IC68.pin16
  N33: IC33.pin17, IC68.pin17
  N34: IC33.pin18, IC68.pin18
  N35: IC33.pin19, IC68.pin19
  N36: IC33.pin20, IC68.pin20
  N37: IC39.pin1, IC59.pin1
  N38: IC39.pin2, IC59.pin2
  N39: IC39.pin3, IC59.pin3
  N40: IC39.pin4, IC59.pin4
  N41: IC39.pin5, IC59.pin5
  N42: IC39.pin6, IC59.pin6
  N43: IC39.pin7, IC59.pin7
  N44: IC39.pin8, IC59.pin8
  N45: IC39.pin9, IC59.pin9
  N46: IC39.pin10, IC59.pin10
  N47: IC39.pin11, IC59.pin11
  N48: IC39.pin12, IC59.pin12
  N49: IC39.pin13, IC59.pin13
  N50: IC39.pin14, IC59.pin14
  N51: IC39.pin15, IC59.pin15
  N52: IC39.pin16, IC59.pin16
  N53: IC39.pin17, IC59.pin17
  N54: IC39.pin18, IC59.pin18
  N55: IC39.pin19, IC59.pin19
  N56: IC39.pin20, IC59.pin20
  N57: IC40.pin1, IC60.pin1
  N58: IC40.pin2, IC60.pin2
  N59: IC40.pin3, IC60.pin3
  N60: IC40.pin4, IC60.pin4
  N61: IC40.pin5, IC60.pin5
  N62: IC40.pin6, IC60.pin6
  N63: IC40.pin7, IC60.pin7
  N64: IC40.pin8, IC60.pin8
  N65: IC40.pin9, IC60.pin9
  N66: IC40.pin10, IC60.pin10
  N67: IC40.pin11, IC60.pin11
  N68: IC40.pin12, IC60.pin12
  N69: IC40.pin13, IC60.pin13
  N70: IC40.pin14, IC60.pin14
  N71: IC40.pin15, IC60.pin15
  N72: IC40.pin16, IC60.pin16
  N73: IC40.pin17, IC60.pin17
  N74: IC40.pin18, IC60.pin18
  N75: IC40.pin19, IC60.pin19
  N76: IC40.pin20, IC60.pin20

notes:
  Middle Layer
  Registers (rs0, rs1, rd)
  ALU - Math Unit
  16-Bit BUS
  Branch
  16-Bit BUS Interfaces
  Clock & Power Interfaces
  rs0 register
  rs1 register
  ALU - Shift Unit
  ALU - Comparator
  Flags Reg
  16-Bit Breadboard Processor
  A
  Y
  BUS>
  B
  Decoder Interfaces
  ALU -Comparator
  Flag Register
  ALU - Shared Control Decoder
  ALU - Math Y Bus Driver
  ALU - Shift Y Bus Driver
  rd register
  <Y
  ALU-OUT (Y) BUS
  rd Out
  ALU Y BUS
  Shared 7408

custom parts:
  Breadboard Split Power: A custom 6 pin per group power supply strip where the top row (ground) is all bussed together and the bottom row (+V) is split in two groups of 12 pins. This version is modified to be a loadable part and was rescaled to be on the standard 1px = 1thou grid with the size set in inches
