# Fritzing sketch Top_Layer (saved by Fritzing 0.9.9b)
breadboards: 12

parts:
  Breadboard11 = Breadboard Split Power  # not connected
  Breadboard12 = Breadboard Split Power  # not connected
  Breadboard13 = Breadboard Split Power  # not connected
  Breadboard14 = Breadboard Split Power  # not connected
  Breadboard15 = Breadboard Split Power  # not connected
  Breadboard16 = Breadboard Split Power  # not connected
  Breadboard17 = Breadboard Split Power  # not connected
  Breadboard18 = Breadboard Split Power  # not connected
  Breadboard19 = Breadboard Split Power  # not connected
  Breadboard20 = Breadboard Split Power  # not connected
  Breadboard21 = Breadboard Split Power  # not connected
  Breadboard22 = Breadboard Split Power  # not connected
  Breadboard23 = Breadboard Split Power  # not connected
  Breadboard24 = Breadboard Split Power  # not connected
  Breadboard25 = Breadboard Split Power  # not connected
  Breadboard26 = Breadboard Split Power  # not connected
  Breadboard27 = Breadboard Split Power  # not connected
  Breadboard28 = Breadboard Split Power  # not connected
  Breadboard29 = Breadboard Split Power  # not connected
  Breadboard30 = Breadboard Split Power  # not connected
  Breadboard31 = Breadboard Split Power  # not connected
  Breadboard32 = Breadboard Split Power  # not connected
  Breadboard33 = Breadboard Split Power  # not connected
  Breadboard34 = Breadboard Split Power  # not connected
  Breadboard62 = Breadboard Split Power  # not connected
  Breadboard63 = Breadboard Split Power  # not connected
  Breadboard64 = Breadboard Split Power  # not connected
  Breadboard65 = Breadboard Split Power  # not connected
  Breadboard66 = Breadboard Split Power  # not connected
  Breadboard67 = Breadboard Split Power  # not connected
  Breadboard68 = Breadboard Split Power  # not connected
  Breadboard69 = Breadboard Split Power  # not connected
  Part1 = Breadboard Power Supply Board SMD  # not connected
  U1 = 555 Timer [package="SO8 [SMD]"]  # not connected
  U2 = 555 Timer [package="SO8 [SMD]"]  # not connected
  U3 = 555 Timer [package="SO8 [SMD]"]  # not connected
  IC12 = IC, DIP package, 28 pins [chip_label=28c256]  # not connected
  IC13 = IC, DIP package, 28 pins [chip_label=28c256]  # not connected
  IC24 = IC, DIP package, 20 pins [chip_label=74273]  # not connected
  Breadboard74 = Breadboard Split Power  # not connected
  Breadboard75 = Breadboard Split Power  # not connected
  Breadboard76 = Breadboard Split Power  # not connected
  Breadboard77 = Breadboard Split Power  # not connected
  Breadboard78 = Breadboard Split Power  # not connected
  Breadboard79 = Breadboard Split Power  # not connected
  Breadboard80 = Breadboard Split Power  # not connected
  Breadboard81 = Breadboard Split Power  # not connected
  Breadboard82 = Breadboard Split Power  # not connected
  Breadboard83 = Breadboard Split Power  # not connected
  Breadboard84 = Breadboard Split Power  # not connected
  Breadboard85 = Breadboard Split Power  # not connected
  IC10 = IC, DIP package, 16 pins [chip_label=74161]  # not connected
  IC11 = IC, DIP package, 16 pins [chip_label=74161]  # not connected
  IC6 = IC, DIP package, 20 pins [chip_label=74273]  # not connected
  IC7 = IC, DIP package, 14 pins [chip_label=7408]  # not connected
  Part2 = Arduino Nano (Rev3.0)  # not connected
  IC25 = IC, DIP package, 20 pins [chip_label=74273]  # not connected
  IC4 = IC, DIP package, 24 pins [chip_label=28c16]  # not connected
  IC9 = IC, DIP package, 16 pins [chip_label=74161]  # not connected
  IC5 = IC, DIP package, 20 pins [chip_label=74273]  # not connected
  IC27 = IC, DIP package, 16 pins [chip_label=74161]  # not connected
  R26 = Resistor [tolerance=±5% resistance=220 package="1206 [SMD]"]
  R28 = Resistor [tolerance=±5% resistance=220 package="1206 [SMD]"]
  R30 = Resistor [tolerance=±5% resistance=220 package="1206 [SMD]"]
  R32 = Resistor [tolerance=±5% resistance=220 package="1206 [SMD]"]
  IC29 = IC, DIP package, 16 pins [chip_label=74161]  # not connected
  U14 = 555 Timer [package="SO8 [SMD]"]  # not connected
  IC30 = IC, DIP package, 16 pins [chip_label=74595]  # not connected
  IC31 = IC, DIP package, 16 pins [chip_label=74595]  # not connected
  IC32 = IC, DIP package, 16 pins [chip_label=74595]  # not connected
  IC33 = IC, DIP package, 16 pins [chip_label=74595]  # not connected
  IC34 = IC, DIP package, 14 pins [chip_label=7408]  # not connected
  IC35 = IC, DIP package, 14 pins [chip_label=7404]  # not connected
  U15 = SWITCH_SPDT [package=kps-1290]  # not connected
  IC36 = IC, DIP package, 20 pins [chip_label=74245]  # not connected
  IC37 = IC, DIP package, 20 pins [chip_label=74245]  # not connected
  IC38 = IC, DIP package, 20 pins [chip_label=74245]  # not connected
  IC39 = IC, DIP package, 20 pins [chip_label=74245]  # not connected
  IC40 = IC, DIP package, 20 pins [chip_label=74244]  # not connected
  IC41 = IC, DIP package, 20 pins [chip_label=74244]  # not connected
  IC42 = IC, DIP package, 16 pins [chip_label=74157]  # not connected
  IC43 = IC, DIP package, 16 pins [chip_label=74253]  # not connected
  IC44 = IC, DIP package, 16 pins [chip_label=74253]  # not connected
  IC45 = IC, DIP package, 16 pins [chip_label=74139]  # not connected
  U16 = 7-SEGMENT-4DIGIT [package=7-segment-4digit]  # not connected
  IC23 = IC, DIP package, 24 pins [chip_label="HM6116 RAM"]  # not connected
  IC46 = IC, DIP package, 24 pins [chip_label="HM6116 RAM"]  # not connected
  R33 = Rotary Potentiometer (Small) [maximum_resistance=100kΩ package=THT]  # not connected
  S1 = Pushbutton [package="[THT]"]
  LED1 = smd LED [color="Yellow (592nm)" package="0603 [SMD]"]  # not connected
  LED2 = smd LED [color="Yellow (592nm)" package="0603 [SMD]"]  # not connected
  LED3 = smd LED [color="Yellow (592nm)" package="0603 [SMD]"]  # not connected
  U17 = SWITCH_SPDT [package=kps-1290]  # not connected
  IC47 = IC, DIP package, 14 pins [chip_label=7432]  # not connected
  IC48 = IC, DIP package, 14 pins [chip_label=7408]
  IC49 = IC, DIP package, 14 pins [chip_label=7404]  # not connected
  LED4 = smd LED [color="Blue (470nm)" package="0603 [SMD]"]

nets:
  N1: R26.Pin_1, R28.Pin_1
  N2: R30.Pin_1, R32.Pin_1
  N3: S1.Pin_1, S1.Pin_2
  N4: S1.Pin_3, S1.Pin_4
  N5: IC48.pin9, LED4.cathode

notes:
  Top Layer
  Master Clock
  Program Counter
  Power Supply
  Program Memory
  Output Display
  Program Memory (ROM)
  Master Clock Module
  Branch Register
  16-Bit BUS
  16-Bit BUS Interfaces
  16-Bit Breadboard Processor
  Clock Bus
  Decoder Interfaces
  Program Memory (RAM)
  Output Data Selector
  INST BUS
  Output Clock
  Arduino PC Interface
  Shared 7408

custom parts:
  Breadboard Split Power: A custom 6 pin per group power supply strip where the top row (ground) is all bussed together and the bottom row (+V) is split in two groups of 12 pins. This version is modified to be a loadable part and was rescaled to be on the standard 1px = 1thou grid with the size set in inches
