// Digital circuit HM6116_2Kx8_RAM.dig as structural Verilog
module HM6116_2Kx8_RAM (
  input  A10,
  input  A9,
  input  A8,
  input  A7,
  input  A6,
  input  A5,
  input  A4,
  input  A3,
  input  A2,
  input  A1,
  input  A0,
  input  nCS,
  input  nW,
  input  nOE,
  input  I_O0,
  input  I_O1,
  input  I_O2,
  input  I_O3,
  input  I_O4,
  input  I_O5,
  input  I_O6,
  input  I_O7,
  input  VCC,
  input  GND
);

  wire and_1_out;
  wire [7:0] ramsingleportsel_d;

  RAMSinglePortSel #(.AddrBits(11), .Bits(8)) ramsingleportsel (
    .A({A10, A9, A8, A7, A6, A5, A4, A3, A2, A1, A0}), .CS(~nCS), .WE(~nW), .OE(~nOE), .D(ramsingleportsel_d));
  and and_1 (and_1_out, ~nCS, nW, ~nOE);  // And
  // Probe on ramsingleportsel_d
  BusSplitter #(.Bits(8)) bussplitter_1 (
    .D(ramsingleportsel_d), .OE(and_1_out), .D0(I_O0), .D1(I_O1), .D2(I_O2), .D3(I_O3), .D4(I_O4), .D5(I_O5),
    .D6(I_O6), .D7(I_O7));

  // Notes on the sheet:
  //   A10: pin 19
  //   A9: pin 22
  //   A8: pin 23
  //   A7: pin 1
  //   A6: pin 2
  //   A5: pin 3
  //   A4: pin 4
  //   A3: pin 5
  //   A2: pin 6
  //   A1: pin 7
  //   A0: pin 8
  //   nCS: pin 18
  //   nW: pin 21, default 1
  //   nOE: pin 20
  //   I_O0: pin 9
  //   I_O1: pin 10
  //   I_O2: pin 11
  //   I_O3: pin 13
  //   I_O4: pin 14
  //   I_O5: pin 15
  //   I_O6: pin 16
  //   I_O7: pin 17
  //   VCC: pin 24
  //   GND: pin 12
endmodule
