// Digital circuit HM6264_64Kx8_RAM.dig as structural Verilog
module HM6264_64Kx8_RAM (
  input  A10,
  input  A9,
  input  A8,
  input  A7,
  input  A6,
  input  A5,
  input  A4,
  input  A3,
  input  A2,
  input  A1,
  input  A0,
  input  nCS1,
  input  nWE,
  input  nOE,
  input  I_O1,
  input  I_O2,
  input  I_O3,
  input  I_O4,
  input  I_O5,
  input  I_O6,
  input  I_O7,
  input  I_O8,
  input  VCC,
  input  GND,
  input  A11,
  input  A12,
  input  NC,
  input  CS2
);

  wire and_1_out, nor_1_out;
  wire [7:0] ramsingleportsel_d;

  nor nor_1 (nor_1_out, CS2, ~nCS1);  // NOr
  RAMSinglePortSel #(.AddrBits(13), .Bits(8)) ramsingleportsel (
    .A({A12, A11, A10, A9, A8, A7, A6, A5, A4, A3, A2, A1, A0}), .CS(~nor_1_out), .WE(~nWE), .OE(~nOE),
    .D(ramsingleportsel_d));
  and and_1 (and_1_out, ~nor_1_out, nWE, ~nOE);  // And
  // Probe on ramsingleportsel_d
  BusSplitter #(.Bits(8)) bussplitter_1 (
    .D(ramsingleportsel_d), .OE(and_1_out), .D0(I_O1), .D1(I_O2), .D2(I_O3), .D3(I_O4), .D4(I_O5), .D5(I_O6),
    .D6(I_O7), .D7(I_O8));

  // Notes on the sheet:
  //   A10: pin 21
  //   A9: pin 24
  //   A8: pin 25
  //   A7: pin 3
  //   A6: pin 4
  //   A5: pin 5
  //   A4: pin 6
  //   A3: pin 7
  //   A2: pin 8
  //   A1: pin 9
  //   A0: pin 10
  //   nCS1: pin 20
  //   nWE: pin 27, default 1
  //   nOE: pin 22
  //   I_O1: pin 11
  //   I_O2: pin 12
  //   I_O3: pin 13
  //   I_O4: pin 15
  //   I_O5: pin 16
  //   I_O6: pin 17
  //   I_O7: pin 18
  //   I_O8: pin 19
  //   VCC: pin 28
  //   GND: pin 14
  //   A11: pin 23
  //   A12: pin 2
  //   NC: pin 1
  //   CS2: pin 26
endmodule
