// Digital circuit ImRegister.dig as structural Verilog
module ImRegister (
  input  D0,
  input  D1,
  input  D2,
  input  D3,
  input  D4,
  input  D5,
  input  D6,
  input  D7,
  input  D8,
  input  D9,
  input  D10,
  input  D11,
  input  D12,
  input  D13,
  input  D14,
  input  D15,
  input  CLK,
  input  IMM,
  input  IMEM,
  output QIMM0,
  output QIMM1,
  output QIMM2,
  output QIMM3,
  output QIMM4,
  output QIMM5,
  output QIMM6,
  output QIMM7,
  output QIMM8,
  output QIMM9,
  output QIMM10,
  output QIMM11,
  output QIMM12,
  output QIMM13,
  output QIMM14,
  output QIMM15,
  output QIMEM0,
  output QIMEM1,
  output QIMEM2,
  output QIMEM3,
  output QIMEM4,
  output QIMEM5,
  output QIMEM6,
  output QIMEM7
);

  wire Quad_2in_OR_pin3;

  _16_Bit_Register _16_bit_register_1 (
    .D0(D0), .D1(D1), .D2(D2), .D3(D3), .D4(D4), .D5(D5), .D6(D6), .D7(D7), .D8(D8), .D9(D9), .D10(D10),
    .D11(D11), .D12(D12), .D13(D13), .D14(D14), .D15(D15), .EN(Quad_2in_OR_pin3), .CLK(CLK), .nCLR(1'b1),
    .Q0(QIMEM0), .Q1(QIMEM1), .Q2(QIMEM2), .Q3(QIMEM3), .Q4(QIMEM4), .Q5(QIMEM5), .Q6(QIMEM6), .Q7(QIMEM7),
    .Q8(QIMM8), .Q9(QIMM9), .Q10(QIMM10), .Q11(QIMM11), .Q12(QIMM12), .Q13(QIMM13), .Q14(QIMM14), .Q15(QIMM15));
  _7432 Quad_2in_OR (
    .pin1(IMM), .pin2(IMEM), .pin3(Quad_2in_OR_pin3), .pin4(1'b0), .pin5(1'b0), .pin7(1'b0), .pin9(1'b0),
    .pin10(1'b0), .pin12(1'b0), .pin13(1'b0), .pin14(1'b1));  // open: pin6, pin8, pin11

  assign QIMM0 = QIMEM0;
  assign QIMM1 = QIMEM1;
  assign QIMM2 = QIMEM2;
  assign QIMM3 = QIMEM3;
  assign QIMM4 = QIMEM4;
  assign QIMM5 = QIMEM5;
  assign QIMM6 = QIMEM6;
  assign QIMM7 = QIMEM7;
endmodule
