// Digital circuit Math-Unit.dig as structural Verilog
module Math_Unit (
  input  A0,
  input  A1,
  input  A2,
  input  A3,
  input  A4,
  input  A5,
  input  A6,
  input  A7,
  input  A8,
  input  A9,
  input  A10,
  input  A11,
  input  A12,
  input  A13,
  input  A14,
  input  A15,
  input  B0,
  input  B1,
  input  B2,
  input  B3,
  input  B4,
  input  B5,
  input  B6,
  input  B7,
  input  B8,
  input  B9,
  input  B10,
  input  B11,
  input  B12,
  input  B13,
  input  B14,
  input  B15,
  input  Ci,
  input  nBOR,
  input  nADDs,
  input  nSUBs,
  input  nANDs,
  input  nORs,
  input  nXOR,
  output Y0,
  output Y1,
  output Y2,
  output Y3,
  output Y4,
  output Y5,
  output Y6,
  output Y7,
  output Y8,
  output Y9,
  output Y10,
  output Y11,
  output Y12,
  output Y13,
  output Y14,
  output Y15,
  output C
);

  wire _74382_1_pin14, _74382_1_pin15, _74382_2_pin14, _74382_3_pin14, BOR, nS0, nS1, nS2, OVR0, OVR1, OVR2,
       OVR3, S0, S1, S2;

  // Probe on {Y15, Y14, Y13, Y12, Y11, Y10, Y9, Y8, Y7, Y6, Y5, Y4, Y3, Y2, Y1, Y0}
  _74382 _74382_1 (
    .pin1(A1), .pin2(B1), .pin3(A0), .pin4(B0), .pin5(S0), .pin6(S1), .pin7(S2), .pin8(Y0), .pin9(Y1),
    .pin10(1'b0), .pin11(Y2), .pin12(Y3), .pin13(OVR0), .pin14(_74382_1_pin14), .pin15(_74382_1_pin15),
    .pin16(B3), .pin17(A3), .pin18(B2), .pin19(A2), .pin20(1'b1));
  _74148 _8_to_3_Pro_Encode (
    .pin1(nXOR), .pin2(nORs), .pin3(nANDs), .pin4(1'b1), .pin5(1'b0), .pin6(nS2), .pin7(nS1), .pin8(1'b0),
    .pin9(nS0), .pin10(1'b1), .pin11(1'b1), .pin12(nSUBs), .pin13(nADDs), .pin16(1'b1));  // open: pin14, pin15
  _7404 Hex_Inv (
    .pin1(nS2), .pin2(S2), .pin3(nS1), .pin4(S1), .pin5(nBOR), .pin6(BOR), .pin7(1'b0), .pin9(1'b0),
    .pin11(1'b0), .pin12(S0), .pin13(nS0), .pin14(1'b1));  // open: pin8, pin10
  _7432 _7432_1 (
    .pin1(1'b0), .pin2(1'b0), .pin4(BOR), .pin5(Ci), .pin6(_74382_1_pin15), .pin7(1'b0), .pin9(1'b0),
    .pin10(1'b0), .pin12(1'b0), .pin13(1'b0), .pin14(1'b1));  // open: pin3, pin8, pin11
  _74382 _74382_2 (
    .pin1(A5), .pin2(B5), .pin3(A4), .pin4(B4), .pin5(S0), .pin6(S1), .pin7(S2), .pin8(Y4), .pin9(Y5),
    .pin10(1'b0), .pin11(Y6), .pin12(Y7), .pin13(OVR1), .pin14(_74382_2_pin14), .pin15(_74382_1_pin14),
    .pin16(B7), .pin17(A7), .pin18(B6), .pin19(A6), .pin20(1'b1));
  _74382 _74382_3 (
    .pin1(A9), .pin2(B9), .pin3(A8), .pin4(B8), .pin5(S0), .pin6(S1), .pin7(S2), .pin8(Y8), .pin9(Y9),
    .pin10(1'b0), .pin11(Y10), .pin12(Y11), .pin13(OVR2), .pin14(_74382_3_pin14), .pin15(_74382_2_pin14),
    .pin16(B11), .pin17(A11), .pin18(B10), .pin19(A10), .pin20(1'b1));
  _74382 _74382_4 (
    .pin1(A13), .pin2(B13), .pin3(A12), .pin4(B12), .pin5(S0), .pin6(S1), .pin7(S2), .pin8(Y12), .pin9(Y13),
    .pin10(1'b0), .pin11(Y14), .pin12(Y15), .pin13(OVR3), .pin14(C), .pin15(_74382_3_pin14), .pin16(B15),
    .pin17(A15), .pin18(B14), .pin19(A14), .pin20(1'b1));

  // Notes on the sheet:
  //   nBOR: default 1
  //   nADDs: default 1
  //   nSUBs: default 1
  //   nANDs: default 1
  //   nORs: default 1
  //   nXOR: default 1
  //   Math Unit Function Table
  //   S2 S1 S0 Operation
  //   L    L    L    000 Clear
  //   L    L    H    001 B - A
  //   L    H   L     010 A - B
  //   L    H   H    011 A + B
  //   H    L   L    100 A XOR B
  //   H    L   H   101 A OR B
  //   H    H  L    110 A AND B
  //   H    H  H   111 Preset
endmodule
