// Digital circuit PC.dig as structural Verilog
module PC (
  input  CLK,
  input  nCLR,
  input  nEN,
  input  nLD,
  input  D15,
  input  D14,
  input  D13,
  input  D12,
  input  D11,
  input  D10,
  input  D9,
  input  D8,
  input  D7,
  input  D6,
  input  D5,
  input  D4,
  input  D3,
  input  D2,
  input  D1,
  input  D0,
  output CO,
  output PC0,
  output PC1,
  output PC2,
  output PC3,
  output PC4,
  output PC5,
  output PC6,
  output PC7,
  output PC8,
  output PC9,
  output PC10,
  output PC11,
  output PC12,
  output PC13,
  output PC14,
  output PC15
);

  wire RCO0, RCO1, RCO2;

  _74161 _74161_1 (
    .pin1(nCLR), .pin2(CLK), .pin3(D0), .pin4(D1), .pin5(D2), .pin6(D3), .pin7(1'b1), .pin8(1'b0),
    .pin9(nLD), .pin10(1'b1), .pin11(PC3), .pin12(PC2), .pin13(PC1), .pin14(PC0), .pin15(RCO0), .pin16(1'b1));
  _74161 _74161_2 (
    .pin1(nCLR), .pin2(CLK), .pin3(D4), .pin4(D5), .pin5(D6), .pin6(D7), .pin7(1'b1), .pin8(1'b0),
    .pin9(nLD), .pin10(RCO0), .pin11(PC7), .pin12(PC6), .pin13(PC5), .pin14(PC4), .pin15(RCO1), .pin16(1'b1));
  _74161 _74161_3 (
    .pin1(nCLR), .pin2(CLK), .pin3(D8), .pin4(D9), .pin5(D10), .pin6(D11), .pin7(1'b1), .pin8(1'b0),
    .pin9(nLD), .pin10(RCO1), .pin11(PC11), .pin12(PC10), .pin13(PC9), .pin14(PC8), .pin15(RCO2), .pin16(1'b1));
  _74161 _74161_4 (
    .pin1(nCLR), .pin2(CLK), .pin3(D12), .pin4(D13), .pin5(D14), .pin6(D15), .pin7(1'b1), .pin8(1'b0),
    .pin9(nLD), .pin10(RCO2), .pin11(PC15), .pin12(PC14), .pin13(PC13), .pin14(PC12), .pin15(CO), .pin16(1'b1));

  // Other names for the same wires on the sheet: Q0[3:0] = {PC3, PC2, PC1, PC0}; Q1[3:0] = {PC7, PC6, PC5, PC4};
  //   Q2[3:0] = {PC11, PC10, PC9, PC8}; Q3[3:0] = {PC15, PC14, PC13, PC12}; D0_t[3:0] = {D3, D2, D1, D0};
  //   D1_t[3:0] = {D7, D6, D5, D4}; D2_t[3:0] = {D11, D10, D9, D8}; D3_t[3:0] = {D15, D14, D13, D12}; RCO3 = CO

  // Notes on the sheet:
  //   CLK: Hz: 20
  //   nCLR: default 1
  //   nLD: default 1
  //   I/O
  //   Program Counter
  //   Inputs
  //   Outputs
endmodule
