// Digital circuit PM.dig as structural Verilog
module PM (
  input  [15:0] A,
  input  nOE,
  input  nCE,
  input  nWE,
  output [15:0] D
);

  // _28c256 PM_ROM0: pin names not known; wires that end beside it: A[14], A[12], A[7], A[6], A[5], A[4], A[3], A[2], A[1], A[0], D[0], D[1], D[2], 1'b0, 1'b1, nWE, A[13], A[8], A[9], A[11], nOE, A[10], nCE, D[7]
  // _28c256 PM_ROM1: pin names not known; wires that end beside it: A[14], A[12], A[7], A[6], A[5], A[4], A[3], A[2], A[1], A[0], D[8], D[9], D[10], 1'b0, 1'b1, nWE, A[13], A[8], A[9], A[11], nOE, A[10], nCE, D[15]
  // also tied to GND on the sheet: A[15]

  // Other names for the same wires on the sheet: DL[7:0] = D[7:0]; DH[7:0] = D[15:8]; AL[7:0] = A[7:0];
  //   AH[7:0] = A[15:8]

  // Notes on the sheet:
  //   nWE: default 1
  //   I/O
  //   Program ROMs
  //   Inputs
  //   Outputs
endmodule
