// Digital circuit Program_Memory_v2.dig as structural Verilog
module Program_Memory_v2 (
  input  A0,
  input  A1,
  input  A2,
  input  A3,
  input  A4,
  input  A5,
  input  A6,
  input  A7,
  input  A8,
  input  A9,
  input  A10,
  input  A11,
  input  nWE,
  input  nOE,
  output D0,
  output D1,
  output D2,
  output D3,
  output D4,
  output D5,
  output D6,
  output D7,
  output D8,
  output D9,
  output D10,
  output D11,
  output D12,
  output D13,
  output D14,
  output D15
);

  wire _7404_1_pin2, _7404_1_pin5, _7404_1_pin6, _74595_1_pin9, _74595_3_pin9, _74595_3_pin14, ARD_A0,
       ARD_A1, ARD_A2, ARD_A3, ARD_A4, ARD_A5, ARD_A6, ARD_A7, ARD_A8, ARD_A9, ARD_A10, ARD_D0, ARD_D1,
       ARD_D2, ARD_D3, ARD_D4, ARD_D5, ARD_D6, ARD_D7, ARD_D8, ARD_D9, ARD_D10, ARD_D11, ARD_D12, ARD_D13,
       ARD_D14, ARD_D15, ARD_OE, ARD_WE, arduino_nano_1_p4, arduino_nano_1_p5, arduino_nano_1_p6,
       arduino_nano_1_p7, arduino_nano_1_p8, nRAM_nOE, nRAM_nWE, nRUN, PROG, RAM_A0, RAM_A1, RAM_A2, RAM_A3,
       RAM_A4, RAM_A5, RAM_A6, RAM_A7, RAM_A8, RAM_A9, RAM_A10;

  DipSwitch PROG_nRUN (.out(PROG));
  _7404 _7404_1 (
    .pin1(ARD_OE), .pin2(_7404_1_pin2), .pin3(1'b0), .pin5(_7404_1_pin5), .pin6(_7404_1_pin6), .pin7(1'b0),
    .pin9(1'b0), .pin11(1'b0), .pin12(nRUN), .pin13(PROG), .pin14(1'b1));  // open: pin4, pin8, pin10
  _7408 _7408_1 (
    .pin1(1'b0), .pin2(1'b0), .pin4(1'b0), .pin5(1'b0), .pin7(1'b0), .pin9(1'b0), .pin10(1'b0),
    .pin11(_7404_1_pin5), .pin12(PROG), .pin13(_7404_1_pin2), .pin14(1'b1));  // open: pin3, pin6, pin8
  // Arduino_Nano arduino_nano_1: pin names not known; wires that end beside it: ARD_WE, 1'b0, ARD_OE, arduino_nano_1_p4, arduino_nano_1_p5, arduino_nano_1_p6, arduino_nano_1_p7, arduino_nano_1_p8
  _74595 _74595_1 (
    .pin1(ARD_D1), .pin2(ARD_D2), .pin3(ARD_D3), .pin4(ARD_D4), .pin5(ARD_D5), .pin6(ARD_D6), .pin7(ARD_D7),
    .pin8(1'b0), .pin9(_74595_1_pin9), .pin10(1'b1), .pin11(arduino_nano_1_p5), .pin12(arduino_nano_1_p4),
    .pin13(1'b0), .pin14(arduino_nano_1_p6), .pin15(ARD_D0), .pin16(1'b1));
  _74595 _74595_2 (
    .pin1(ARD_D9), .pin2(ARD_D10), .pin3(ARD_D11), .pin4(ARD_D12), .pin5(ARD_D13), .pin6(ARD_D14),
    .pin7(ARD_D15), .pin8(1'b0), .pin10(1'b1), .pin11(arduino_nano_1_p5), .pin12(arduino_nano_1_p4),
    .pin13(1'b0), .pin14(_74595_1_pin9), .pin15(ARD_D8), .pin16(1'b1));  // open: pin9
  _74595 _74595_3 (
    .pin1(ARD_A1), .pin2(ARD_A2), .pin3(ARD_A3), .pin4(ARD_A4), .pin5(ARD_A5), .pin6(ARD_A6), .pin7(ARD_A7),
    .pin8(1'b0), .pin9(_74595_3_pin9), .pin10(1'b1), .pin11(arduino_nano_1_p8), .pin12(arduino_nano_1_p7),
    .pin13(1'b0), .pin14(_74595_3_pin14), .pin15(ARD_A0), .pin16(1'b1));
  _74595 _74595_4 (
    .pin1(ARD_A9), .pin2(ARD_A10), .pin8(1'b0), .pin10(1'b1), .pin11(arduino_nano_1_p8),
    .pin12(arduino_nano_1_p7), .pin13(1'b0), .pin14(_74595_3_pin9), .pin15(ARD_A8), .pin16(1'b1));  // open: pin3, pin4, pin5, pin6, pin7, pin9
  _74245 _74245_1 (
    .pin1(1'b1), .pin2(ARD_D0), .pin3(ARD_D1), .pin4(ARD_D2), .pin5(ARD_D3), .pin6(ARD_D4), .pin7(ARD_D5),
    .pin8(ARD_D6), .pin9(ARD_D7), .pin10(1'b0), .pin11(D7), .pin12(D6), .pin13(D5), .pin14(D4), .pin15(D3),
    .pin16(D2), .pin17(D1), .pin18(D0), .pin19(_7404_1_pin6), .pin20(1'b1));
  _74245 _74245_2 (
    .pin1(1'b1), .pin2(ARD_D8), .pin3(ARD_D9), .pin4(ARD_D10), .pin5(ARD_D11), .pin6(ARD_D12),
    .pin7(ARD_D13), .pin8(ARD_D14), .pin9(ARD_D15), .pin10(1'b0), .pin11(D15), .pin12(D14), .pin13(D13),
    .pin14(D12), .pin15(D11), .pin16(D10), .pin17(D9), .pin18(D8), .pin19(_7404_1_pin6), .pin20(1'b1));
  _74245 _74245_3 (
    .pin1(1'b1), .pin2(ARD_A0), .pin3(ARD_A1), .pin4(ARD_A2), .pin5(ARD_A3), .pin6(ARD_A4), .pin7(ARD_A5),
    .pin8(ARD_A6), .pin9(ARD_A7), .pin10(1'b0), .pin11(RAM_A7), .pin12(RAM_A6), .pin13(RAM_A5),
    .pin14(RAM_A4), .pin15(RAM_A3), .pin16(RAM_A2), .pin17(RAM_A1), .pin18(RAM_A0), .pin19(_7404_1_pin6),
    .pin20(1'b1));
  _74245 _74245_4 (
    .pin1(1'b1), .pin2(ARD_A8), .pin3(ARD_A9), .pin4(ARD_A10), .pin5(1'b0), .pin6(1'b0), .pin7(1'b0),
    .pin8(1'b0), .pin9(1'b0), .pin10(1'b0), .pin16(RAM_A10), .pin17(RAM_A9), .pin18(RAM_A8),
    .pin19(_7404_1_pin6), .pin20(1'b1));  // open: pin11, pin12, pin13, pin14, pin15
  _74245 _74245_5 (
    .pin1(1'b1), .pin2(A0), .pin3(A1), .pin4(A2), .pin5(A3), .pin6(A4), .pin7(A5), .pin8(A6), .pin9(A7),
    .pin10(1'b0), .pin11(RAM_A7), .pin12(RAM_A6), .pin13(RAM_A5), .pin14(RAM_A4), .pin15(RAM_A3),
    .pin16(RAM_A2), .pin17(RAM_A1), .pin18(RAM_A0), .pin19(nRUN), .pin20(1'b1));
  _74245 _74245_6 (
    .pin1(1'b1), .pin2(A8), .pin3(A9), .pin4(A10), .pin5(1'b0), .pin6(1'b0), .pin7(1'b0), .pin8(1'b0),
    .pin9(1'b0), .pin10(1'b0), .pin16(RAM_A10), .pin17(RAM_A9), .pin18(RAM_A8), .pin19(nRUN), .pin20(1'b1));  // open: pin11, pin12, pin13, pin14, pin15
  _74157 _74157_1 (
    .pin1(nRUN), .pin2(ARD_WE), .pin3(nWE), .pin4(nRAM_nWE), .pin5(ARD_OE), .pin6(nOE), .pin7(nRAM_nOE),
    .pin8(1'b0), .pin10(1'b0), .pin11(1'b0), .pin13(1'b0), .pin14(1'b0), .pin15(nRUN), .pin16(1'b1));  // open: pin9, pin12
  HM6116_2Kx8_RAM hm6116_2kx8_ram_1 (
    .A10(RAM_A10), .A9(RAM_A9), .A8(RAM_A8), .A7(RAM_A7), .A6(RAM_A6), .A5(RAM_A5), .A4(RAM_A4), .A3(RAM_A3),
    .A2(RAM_A2), .A1(RAM_A1), .A0(RAM_A0), .nCS(1'b0), .nW(nRAM_nWE), .nOE(nRAM_nOE), .I_O0(D0), .I_O1(D1),
    .I_O2(D2), .I_O3(D3), .I_O4(D4), .I_O5(D5), .I_O6(D6), .I_O7(D7), .VCC(1'b1), .GND(1'b0));
  HM6116_2Kx8_RAM hm6116_2kx8_ram_2 (
    .A10(RAM_A10), .A9(RAM_A9), .A8(RAM_A8), .A7(RAM_A7), .A6(RAM_A6), .A5(RAM_A5), .A4(RAM_A4), .A3(RAM_A3),
    .A2(RAM_A2), .A1(RAM_A1), .A0(RAM_A0), .nCS(1'b0), .nW(nRAM_nWE), .nOE(nRAM_nOE), .I_O0(D8), .I_O1(D9),
    .I_O2(D10), .I_O3(D11), .I_O4(D12), .I_O5(D13), .I_O6(D14), .I_O7(D15), .VCC(1'b1), .GND(1'b0));

  // Other names for the same wires on the sheet: MEM_A0 = A0; MEM_A1 = A1; MEM_A2 = A2; MEM_A3 = A3; MEM_A4 = A4;
  //   MEM_A5 = A5; MEM_A6 = A6; MEM_A7 = A7; MEM_A8 = A8; MEM_A9 = A9; MEM_A10 = A10; MEM_A11 = A11; MEM_OE = nOE;
  //   MEM_WE = nWE; RAM_I_O0 = D0; RAM_I_O1 = D1; RAM_I_O2 = D2; RAM_I_O3 = D3; RAM_I_O4 = D4; RAM_I_O5 = D5;
  //   RAM_I_O6 = D6; RAM_I_O7 = D7; RAM_I_O8 = D8; RAM_I_O9 = D9; RAM_I_O10 = D10; RAM_I_O11 = D11; RAM_I_O12 = D12;
  //   RAM_I_O13 = D13; RAM_I_O14 = D14; RAM_I_O15 = D15

  // Notes on the sheet:
  //   ARD-ADDR DRIVERS (11)
  //   ARD-DATA DRIVERS (16)
  //   MEM-ADDR DRIVERS (11)
endmodule
