// Digital circuit RAM.dig as structural Verilog
module RAM (
  input  D0,
  input  D1,
  input  D2,
  input  D3,
  input  D4,
  input  D5,
  input  D6,
  input  D7,
  input  D8,
  input  D9,
  input  D10,
  input  D11,
  input  D12,
  input  D13,
  input  D14,
  input  D15,
  input  nWE,
  input  nOE,
  input  nCE,
  input  A0,
  input  A1,
  input  A2,
  input  A3,
  input  A4,
  input  A5,
  input  A6,
  input  A7
);

  HM6116_2Kx8_RAM HI (
    .A10(1'b0), .A9(1'b0), .A8(1'b0), .A7(A7), .A6(A6), .A5(A5), .A4(A4), .A3(A3), .A2(A2), .A1(A1), .A0(A0),
    .nCS(nCE), .nW(nWE), .nOE(nOE), .I_O0(D8), .I_O1(D9), .I_O2(D10), .I_O3(D11), .I_O4(D12), .I_O5(D13),
    .I_O6(D14), .I_O7(D15), .VCC(1'b1), .GND(1'b0));
  HM6116_2Kx8_RAM LO (
    .A10(1'b0), .A9(1'b0), .A8(1'b0), .A7(A7), .A6(A6), .A5(A5), .A4(A4), .A3(A3), .A2(A2), .A1(A1), .A0(A0),
    .nCS(nCE), .nW(nWE), .nOE(nOE), .I_O0(D0), .I_O1(D1), .I_O2(D2), .I_O3(D3), .I_O4(D4), .I_O5(D5),
    .I_O6(D6), .I_O7(D7), .VCC(1'b1), .GND(1'b0));

  // Notes on the sheet:
  //   nWE: default 1
  //   nOE: default 1
  //   RAM Addressing
  //   256 Words in Lo Memory Bank (Addr[0:FF])
  //   Mem Word: 16-Bit
  //   Mem Addr: 8-Bit
endmodule
