// Digital circuit Shift-Unit.dig as structural Verilog
module Shift_Unit (
  input  A0,
  input  A1,
  input  A2,
  input  A3,
  input  A4,
  input  A5,
  input  A6,
  input  A7,
  input  A8,
  input  A9,
  input  A10,
  input  A11,
  input  A12,
  input  A13,
  input  A14,
  input  A15,
  input  nCLR,
  input  CLK,
  input  nSLL,
  input  nSRL,
  input  nROR,
  input  nROL,
  input  nSLD,
  output Y0,
  output Y1,
  output Y2,
  output Y3,
  output Y4,
  output Y5,
  output Y6,
  output Y7,
  output Y8,
  output Y9,
  output Y10,
  output Y11,
  output Y12,
  output Y13,
  output Y14,
  output Y15
);

  wire HI_pin17, HI_pin18, LO_pin8, LO_pin11, LO_pin17, LO_pin18, nS0, nS1, nSLLs, nSRLs, ROL, ROR, S0, S1,
       SLD;

  _7408 _4x2xAND (
    .pin1(nSLL), .pin2(nROL), .pin3(nSLLs), .pin4(nSRL), .pin5(nROR), .pin6(nSRLs), .pin7(1'b0), .pin9(1'b0),
    .pin10(1'b0), .pin12(1'b0), .pin13(1'b0), .pin14(1'b1));  // open: pin8, pin11
  // Probe on {Y15, Y14, Y13, Y12, Y11, Y10, Y9, Y8, Y7, Y6, Y5, Y4, Y3, Y2, Y1, Y0}
  _74148 _8_to_3_Pro_Encode (
    .pin1(1'b1), .pin2(1'b1), .pin3(1'b1), .pin4(1'b1), .pin5(1'b0), .pin7(nS1), .pin8(1'b0), .pin9(nS0),
    .pin10(1'b1), .pin11(nSLLs), .pin12(nSRLs), .pin13(nSLD), .pin16(1'b1));  // open: pin6, pin14, pin15
  _7404 Hex_Inv (
    .pin1(nS0), .pin2(S0), .pin3(nS1), .pin4(S1), .pin5(nSLD), .pin6(SLD), .pin7(1'b0), .pin8(ROR),
    .pin9(nROR), .pin10(ROL), .pin11(nROL), .pin13(1'b0), .pin14(1'b1));  // open: pin12
  _74245 _74245_1 (
    .pin1(1'b1), .pin2(A0), .pin3(A1), .pin4(A2), .pin5(A3), .pin6(A4), .pin7(A5), .pin8(A6), .pin9(A7),
    .pin10(1'b0), .pin11(Y7), .pin12(Y6), .pin13(Y5), .pin14(Y4), .pin15(Y3), .pin16(Y2), .pin17(Y1),
    .pin18(Y0), .pin19(nSLD), .pin20(1'b1));
  _74245 _74245_2 (
    .pin1(1'b1), .pin2(A8), .pin3(A9), .pin4(A10), .pin5(A11), .pin6(A12), .pin7(A13), .pin8(A14),
    .pin9(A15), .pin10(1'b0), .pin11(Y15), .pin12(Y14), .pin13(Y13), .pin14(Y12), .pin15(Y11), .pin16(Y10),
    .pin17(Y9), .pin18(Y8), .pin19(nSLD), .pin20(1'b1));
  _74299 LO (
    .pin1(S0), .pin2(SLD), .pin3(SLD), .pin4(Y6), .pin5(Y4), .pin6(Y2), .pin7(Y0), .pin8(LO_pin8),
    .pin9(nCLR), .pin10(1'b0), .pin11(LO_pin11), .pin12(CLK), .pin13(Y1), .pin14(Y3), .pin15(Y5), .pin16(Y7),
    .pin17(LO_pin17), .pin18(LO_pin18), .pin19(S1), .pin20(1'b1));
  _74299 HI (
    .pin1(S0), .pin2(SLD), .pin3(SLD), .pin4(Y14), .pin5(Y12), .pin6(Y10), .pin7(Y8), .pin8(LO_pin18),
    .pin9(nCLR), .pin10(1'b0), .pin11(LO_pin17), .pin12(CLK), .pin13(Y9), .pin14(Y11), .pin15(Y13),
    .pin16(Y15), .pin17(HI_pin17), .pin18(HI_pin18), .pin19(S1), .pin20(1'b1));
  _7408 _4x2xAND_2 (
    .pin1(ROR), .pin2(LO_pin8), .pin3(HI_pin18), .pin4(ROL), .pin5(HI_pin17), .pin6(LO_pin11), .pin7(1'b0),
    .pin9(1'b0), .pin10(1'b0), .pin12(1'b0), .pin13(1'b0), .pin14(1'b1));  // open: pin8, pin11

  // Other names for the same wires on the sheet: I_O0 = Y0; I_O1 = Y1; I_O2 = Y2; I_O3 = Y3; I_O4 = Y4; I_O5 = Y5;
  //   I_O6 = Y6; I_O7 = Y7; I_O8 = Y8; I_O9 = Y9; I_O10 = Y10; I_O11 = Y11; I_O12 = Y12; I_O13 = Y13; I_O14 = Y14;
  //   I_O15 = Y15

  // Notes on the sheet:
  //   nCLR: default 1
  //   nSLL: default 1
  //   nSRL: default 1
  //   nROR: default 1
  //   nROL: default 1
  //   nSLD: default 1
  //   SLL && ROL
  //   SRL && ROR
  //   16-Bit Shift Register PIPO - Separate Ports
  //   Input drivers required to support
  //   shift register bidirectional
  //   ports for shift load operation
endmodule
