// Digital circuit Test_74148_8-to-3_Encode.dig as structural Verilog
module Test_74148_8_to_3_Encode (
  input  in_1,
  input  in_2,
  input  in_3,
  input  in_4,
  input  in_5,
  input  in_6,
  input  in_7,
  input  in_8,
  input  in_9,
  output out_10,
  output out_11
);

  wire A0, A1, A2;

  _74148 _8_to_3_Pro_Encode (
    .pin1(in_1), .pin2(in_2), .pin3(in_3), .pin4(in_4), .pin5(in_5), .pin6(A2), .pin7(A1), .pin8(1'b0),
    .pin9(A0), .pin10(in_9), .pin11(in_8), .pin12(in_7), .pin13(in_6), .pin14(out_11), .pin15(out_10),
    .pin16(1'b1));
  LED led_1 (.in(A2));
  LED led_2 (.in(A0));
  LED led_3 (.in(A1));
endmodule
